// Logisim project AVR.circ as structural Verilog
module CORE (
);

  wire alu_1_sreg_en, not_1_out;
  wire [2:0] instr_reg_1_bits_out, or_5_out;
  wire [5:0] bit_extender_3_out, or_4_out;
  wire [7:0] alu_1_result, alu_1_sreg_out, controlled_buffer_1_out, controlled_buffer_4_out,
       instr_reg_1_immediate_out, iomem_1_sreg_out, or_2_out, progcounter_1_pc_2_out,
       progcounter_1_pc_2_out_2, pull_resistor_1_node, pull_resistor_4_node, registerfilev2_1_rd_out,
       registerfilev2_1_rr_out;
  wire [9:0] bit_extender_1_out;
  wire [10:0] bit_extender_2_out;
  wire [15:0] flash_1_data_out, instr_reg_1_out_4, instr_reg_1_params_out, iomem_1_sp_out, or_1_out,
       progcounter_1_pc_out, registerfilev2_1_reg_pair_out;
  wire [31:0] decoder_1_con1, decoder_1_con2;

  Decoder decoder_1 (.in_1(instr_reg_1_out_4), .CON2(decoder_1_con2), .CON1(decoder_1_con1));
  assign controlled_buffer_1_out = decoder_1_con2[26] ? progcounter_1_pc_2_out : 8'bz;  // Controlled_Buffer controlled_buffer_1
  assign controlled_buffer_1_out = decoder_1_con2[27] ? progcounter_1_pc_2_out_2 : 8'bz;  // Controlled_Buffer controlled_buffer_2
  FLASH flash_1 (
    .PC_IN(progcounter_1_pc_out), .Indirect_IN(registerfilev2_1_reg_pair_out), .DATA_OUT(flash_1_data_out));
  Instr_Reg instr_reg_1 (
    .in_1(flash_1_data_out), .out_4(instr_reg_1_out_4), .in_2(decoder_1_con1),
    .Params_OUT(instr_reg_1_params_out), .Immediate_OUT(instr_reg_1_immediate_out),
    .Bits_OUT(instr_reg_1_bits_out));
  ProgCounter progcounter_1 (
    .PC_OUT(progcounter_1_pc_out), .Indirect_IN(registerfilev2_1_reg_pair_out),
    .Data_IN(controlled_buffer_1_out), .Relative_Offset(instr_reg_1_params_out), .CONTROL(decoder_1_con1),
    .Bit_to_check(instr_reg_1_bits_out), .BRBC(decoder_1_con2[7]), .BRBS(decoder_1_con2[8]),
    .PC_2_OUT({progcounter_1_pc_2_out_2, progcounter_1_pc_2_out}));
  Bit_Extender #(.in_width(16), .out_width(10)) bit_extender_1 (.in(instr_reg_1_params_out), .out(bit_extender_1_out));
  assign or_1_out = iomem_1_sp_out | instr_reg_1_params_out | registerfilev2_1_reg_pair_out;  // OR_Gate or_1, 16 bits wide
  Bit_Extender #(.in_width(16), .out_width(11)) bit_extender_2 (.in(or_1_out), .out(bit_extender_2_out));
  ALU alu_1 (
    .Rd(registerfilev2_1_rd_out), .Rr(or_2_out), .RESULT(alu_1_result), .OP(decoder_1_con1[21:18]),
    .SREG_OUT(alu_1_sreg_out), .SREG_IN(iomem_1_sreg_out), .SREG_EN(alu_1_sreg_en));
  SRAM sram_1 (
    .Addr_IN(bit_extender_2_out), .Data_IN(controlled_buffer_1_out), .DATA_OUT(controlled_buffer_1_out),
    .Write(decoder_1_con2[24]), .Read(decoder_1_con2[25]));
  RegisterFileV2 registerfilev2_1 (
    .Reg_Pair_OUT(registerfilev2_1_reg_pair_out), .DATA_IN(controlled_buffer_1_out),
    .Rd_Addr(bit_extender_1_out), .Rd_OUT(registerfilev2_1_rd_out), .Rr_OUT(registerfilev2_1_rr_out),
    .CONTROL(decoder_1_con1), .Bit_to_set(instr_reg_1_bits_out), .Bit_Load(decoder_1_con2[5]),
    .Bit_to_read(decoder_1_con2[4:2]));
  not not_1 (not_1_out, decoder_1_con1[22]);
  Pull_Resistor pull_resistor_1 (.node(pull_resistor_1_node));
  assign pull_resistor_1_node = not_1_out ? registerfilev2_1_rr_out : 8'bz;  // Controlled_Buffer controlled_buffer_3
  assign or_2_out = instr_reg_1_immediate_out | pull_resistor_1_node;  // OR_Gate or_2, 8 bits wide
  // Probe on controlled_buffer_1_out
  Bit_Extender #(.in_width(10), .out_width(6)) bit_extender_3 (.in(bit_extender_1_out), .out(bit_extender_3_out));
  assign controlled_buffer_4_out = decoder_1_con2[23] ? registerfilev2_1_rd_out : 8'bz;  // Controlled_Buffer controlled_buffer_4
  assign controlled_buffer_1_out = alu_1_result | controlled_buffer_4_out | pull_resistor_4_node;  // OR_Gate or_3, 8 bits wide
  Pull_Resistor pull_resistor_2 (.node(controlled_buffer_4_out));
  Pull_Resistor pull_resistor_3 (.node(alu_1_result));
  Pull_Resistor pull_resistor_4 (.node(pull_resistor_4_node));
  assign or_4_out = bit_extender_3_out | decoder_1_con2[14:9];  // OR_Gate or_4, 6 bits wide
  assign or_5_out = decoder_1_con2[19:17] | instr_reg_1_bits_out;  // OR_Gate or_5, 3 bits wide
  IOMem iomem_1 (
    .Address(or_4_out), .DATA_IN(controlled_buffer_1_out), .DATA_OUT(pull_resistor_4_node),
    .Write(decoder_1_con2[15]), .Read(decoder_1_con2[16]), .BitToMod(or_5_out), .BM_CLR(decoder_1_con2[20]),
    .BM_SET(decoder_1_con2[21]), .SREG_IN(alu_1_sreg_out), .SREG_ALU_EN(alu_1_sreg_en),
    .SREG_OUT(iomem_1_sreg_out), .SREG_LDT(decoder_1_con2[22]), .SP_OUT(iomem_1_sp_out),
    .SP_Push(decoder_1_con2[29]), .SP_Pop(decoder_1_con2[28]));
endmodule

module ALU (
  input  [7:0] SREG_IN,
  input  [3:0] OP,
  input  [7:0] Rd,
  input  [7:0] Rr,
  output [7:0] SREG_OUT,
  output SREG_EN,
  output [7:0] RESULT
);

  wire and_1_flags_enable_2, com_1_flags_enable_2, decoder_1_out0, decoder_1_out1, decoder_1_out2,
       decoder_1_out3, decoder_1_out4, decoder_1_out5, decoder_1_out6, decoder_1_out7, decoder_1_out8,
       decoder_1_out9, decoder_1_out10, decoder_1_out11, decoder_1_out12, decoder_1_out13, decoder_1_out14,
       eor_1_flags_enable_2, neg_1_flags_enable_2, not_1_out, or_1_flags_enable_2, shift_1_flags_enable_2,
       subtractor_1_flags_enable_2;
  wire [7:0] adder_1_data_bus_out, and_1_data_bus_out, and_1_flags_out, com_1_data_bus_out, com_1_flags_out,
       eor_1_data_bus_out, eor_1_flags_out, neg_1_data_bus_out, neg_1_flags_out, or_1_data_bus_out,
       or_1_flags_out, shift_1_data_bus_out, shift_1_flags_out, subtractor_1_data_bus_out,
       subtractor_1_flags_out;

  assign RESULT = decoder_1_out0 ? Rr : 8'bz;  // Controlled_Buffer controlled_buffer_1
  not not_1 (not_1_out, decoder_1_out0);
  assign RESULT = not_1_out ? adder_1_data_bus_out : 8'bz;  // Controlled_Buffer controlled_buffer_2
  ADDER adder_1 (
    .Rd(Rd), .Rr(Rr), .DATA_BUS_OUT(adder_1_data_bus_out), .DATA_BUS_IN(and_1_data_bus_out),
    .ADD(decoder_1_out1), .ADC(decoder_1_out2), .FLAGS_IN(and_1_flags_out), .FLAGS_OUT(SREG_OUT),
    .FLAGS_ENABLE_2(SREG_EN), .FLAGS_ENABLE(and_1_flags_enable_2));
  AND and_1 (
    .FLAGS_OUT(and_1_flags_out), .FLAGS_ENABLE_2(and_1_flags_enable_2), .DATA_BUS_OUT(and_1_data_bus_out),
    .AND(decoder_1_out3), .FLAGS_IN(shift_1_flags_out), .FLAGS_ENABLE(shift_1_flags_enable_2),
    .DATA_BUS_IN(shift_1_data_bus_out), .Rd(Rd), .Rr(Rr));
  SHIFT shift_1 (
    .Rd(Rd), .FLAGS_OUT(shift_1_flags_out), .FLAGS_ENABLE_2(shift_1_flags_enable_2),
    .DATA_BUS_OUT(shift_1_data_bus_out), .LSL(decoder_1_out4), .FLAGS_IN(subtractor_1_flags_out),
    .FLAGS_ENABLE(subtractor_1_flags_enable_2), .DATA_BUS_IN(subtractor_1_data_bus_out),
    .LSR(decoder_1_out5), .ROL(decoder_1_out6), .ROR(decoder_1_out7), .ASR(decoder_1_out8));
  SUBTRACTOR subtractor_1 (
    .FLAGS_OUT(subtractor_1_flags_out), .FLAGS_ENABLE_2(subtractor_1_flags_enable_2),
    .DATA_BUS_OUT(subtractor_1_data_bus_out), .Rd(Rd), .Rr(Rr), .SUB(decoder_1_out9), .SBC(decoder_1_out10),
    .FLAGS_IN(or_1_flags_out), .FLAGS_ENABLE(or_1_flags_enable_2), .DATA_BUS_IN(or_1_data_bus_out));
  OR or_1 (
    .FLAGS_OUT(or_1_flags_out), .FLAGS_ENABLE_2(or_1_flags_enable_2), .DATA_BUS_OUT(or_1_data_bus_out),
    .Rd(Rd), .OR(decoder_1_out11), .Rr(Rr), .FLAGS_IN(eor_1_flags_out), .FLAGS_ENABLE(eor_1_flags_enable_2),
    .DATA_BUS_IN(eor_1_data_bus_out));
  EOR eor_1 (
    .Rd(Rd), .Rr(Rr), .EOR(decoder_1_out12), .FLAGS_OUT(eor_1_flags_out),
    .FLAGS_ENABLE_2(eor_1_flags_enable_2), .DATA_BUS_OUT(eor_1_data_bus_out), .FLAGS_IN(com_1_flags_out),
    .FLAGS_ENABLE(com_1_flags_enable_2), .DATA_BUS_IN(com_1_data_bus_out));
  COM com_1 (
    .Rd(Rd), .COM(decoder_1_out13), .FLAGS_OUT(com_1_flags_out), .FLAGS_ENABLE_2(com_1_flags_enable_2),
    .DATA_BUS_OUT(com_1_data_bus_out), .FLAGS_IN(neg_1_flags_out), .FLAGS_ENABLE(neg_1_flags_enable_2),
    .DATA_BUS_IN(neg_1_data_bus_out));
  NEG neg_1 (
    .Rd(Rd), .COM(decoder_1_out14), .FLAGS_OUT(neg_1_flags_out), .FLAGS_ENABLE_2(neg_1_flags_enable_2),
    .DATA_BUS_OUT(neg_1_data_bus_out), .FLAGS_IN(SREG_IN), .FLAGS_ENABLE(1'b0), .DATA_BUS_IN({8{1'b0}}));
  Decoder_part #(.select(4)) decoder_1 (
    .out0(decoder_1_out0), .out1(decoder_1_out1), .out2(decoder_1_out2), .out3(decoder_1_out3),
    .out4(decoder_1_out4), .out5(decoder_1_out5), .out6(decoder_1_out6), .out7(decoder_1_out7),
    .out8(decoder_1_out8), .out9(decoder_1_out9), .out10(decoder_1_out10), .out11(decoder_1_out11),
    .out12(decoder_1_out12), .out13(decoder_1_out13), .out14(decoder_1_out14), .sel(OP), .en(1'b1));  // open: out15
endmodule

// ADD
module ADDER (
  input  [7:0] Rd,
  input  [7:0] Rr,
  input  ADD,
  input  ADC,
  input  [7:0] FLAGS_IN,
  input  FLAGS_ENABLE,
  input  [7:0] DATA_BUS_IN,
  output [7:0] FLAGS_OUT,
  output FLAGS_ENABLE_2,
  output [7:0] DATA_BUS_OUT
);

  wire adder_1_cout, adder_2_cout, and_1_out, and_2_out, comparator_1_eq, controlled_buffer_7_out, not_4_out,
       or_1_out, or_4_out, xor_1_out;
  wire [3:0] not_2_out, not_3_out;
  wire [7:0] adder_1_out, not_1_out, pull_resistor_1_node;

  assign not_1_out = ~adder_1_out;  // NOT_Gate not_1, 8 bits wide
  and and_1 (and_1_out, Rd[7], Rr[7], not_1_out[7]);
  or or_1 (or_1_out, and_1_out, and_2_out);
  assign not_2_out = ~Rd[7:4];  // NOT_Gate not_2, 4 bits wide
  assign not_3_out = ~Rr[7:4];  // NOT_Gate not_3, 4 bits wide
  and and_2 (and_2_out, not_2_out[3], not_3_out[3], adder_1_out[7]);
  Adder #(.width(4)) adder_1 (
    .a(Rd[3:0]), .b(Rr[3:0]), .out(adder_1_out[3:0]), .cin(controlled_buffer_7_out), .cout(adder_1_cout));
  Adder #(.width(4)) adder_2 (
    .a(Rd[7:4]), .b(Rr[7:4]), .out(adder_1_out[7:4]), .cin(adder_1_cout), .cout(adder_2_cout));
  assign FLAGS_OUT[0] = or_4_out ? adder_2_cout : 1'bz;  // Controlled_Buffer controlled_buffer_1
  assign FLAGS_OUT[1] = or_4_out ? comparator_1_eq : 1'bz;  // Controlled_Buffer controlled_buffer_2
  assign FLAGS_OUT[2] = or_4_out ? adder_1_out[7] : 1'bz;  // Controlled_Buffer controlled_buffer_3
  assign FLAGS_OUT[3] = or_4_out ? or_1_out : 1'bz;  // Controlled_Buffer controlled_buffer_4
  assign FLAGS_OUT[4] = or_4_out ? xor_1_out : 1'bz;  // Controlled_Buffer controlled_buffer_5
  assign FLAGS_OUT[5] = or_4_out ? adder_1_cout : 1'bz;  // Controlled_Buffer controlled_buffer_6
  xor xor_1 (xor_1_out, FLAGS_OUT[3], FLAGS_OUT[2]);
  assign controlled_buffer_7_out = ADC ? FLAGS_IN[0] : 1'bz;  // Controlled_Buffer controlled_buffer_7
  Comparator comparator_1 (.a(adder_1_out), .b({8{1'b0}}), .eq(comparator_1_eq));  // open: gt, lt
  assign FLAGS_OUT[4] = not_4_out ? FLAGS_IN[4] : 1'bz;  // Controlled_Buffer controlled_buffer_8
  assign FLAGS_OUT[1] = not_4_out ? FLAGS_IN[1] : 1'bz;  // Controlled_Buffer controlled_buffer_9
  assign FLAGS_OUT[0] = not_4_out ? FLAGS_IN[0] : 1'bz;  // Controlled_Buffer controlled_buffer_10
  assign FLAGS_OUT[2] = not_4_out ? FLAGS_IN[2] : 1'bz;  // Controlled_Buffer controlled_buffer_11
  assign FLAGS_OUT[5] = not_4_out ? FLAGS_IN[5] : 1'bz;  // Controlled_Buffer controlled_buffer_12
  assign FLAGS_OUT[3] = not_4_out ? FLAGS_IN[3] : 1'bz;  // Controlled_Buffer controlled_buffer_13
  or or_2 (FLAGS_ENABLE_2, FLAGS_ENABLE, or_4_out);
  not not_4 (not_4_out, or_4_out);
  assign DATA_BUS_OUT = pull_resistor_1_node | DATA_BUS_IN;  // OR_Gate or_3, 8 bits wide
  Pull_Resistor pull_resistor_1 (.node(pull_resistor_1_node));
  assign pull_resistor_1_node = or_4_out ? adder_1_out : 8'bz;  // Controlled_Buffer controlled_buffer_14
  or or_4 (or_4_out, ADC, ADD);

  assign FLAGS_OUT[7:6] = FLAGS_IN[7:6];
endmodule

module AND (
  input  [7:0] Rd,
  input  AND,
  input  [7:0] Rr,
  input  [7:0] FLAGS_IN,
  input  FLAGS_ENABLE,
  input  [7:0] DATA_BUS_IN,
  output [7:0] FLAGS_OUT,
  output FLAGS_ENABLE_2,
  output [7:0] DATA_BUS_OUT
);

  wire comparator_1_eq, not_1_out, xor_1_out;
  wire [7:0] and_1_out, pull_resistor_2_node;

  assign and_1_out = Rd & Rr;  // AND_Gate and_1, 8 bits wide
  assign FLAGS_OUT[2] = AND ? and_1_out[7] : 1'bz;  // Controlled_Buffer controlled_buffer_1
  assign FLAGS_OUT[4] = AND ? xor_1_out : 1'bz;  // Controlled_Buffer controlled_buffer_2
  xor xor_1 (xor_1_out, and_1_out[7], FLAGS_OUT[3]);
  assign FLAGS_OUT[4] = not_1_out ? FLAGS_IN[4] : 1'bz;  // Controlled_Buffer controlled_buffer_3
  Comparator comparator_1 (.a(and_1_out), .b({8{1'b0}}), .eq(comparator_1_eq));  // open: gt, lt
  Pull_Resistor pull_resistor_1 (.node(FLAGS_OUT[3]));
  assign FLAGS_OUT[2] = not_1_out ? FLAGS_IN[2] : 1'bz;  // Controlled_Buffer controlled_buffer_4
  assign FLAGS_OUT[1] = not_1_out ? FLAGS_IN[1] : 1'bz;  // Controlled_Buffer controlled_buffer_5
  assign FLAGS_OUT[3] = not_1_out ? FLAGS_IN[3] : 1'bz;  // Controlled_Buffer controlled_buffer_6
  or or_1 (FLAGS_ENABLE_2, FLAGS_ENABLE, AND);
  assign FLAGS_OUT[1] = AND ? comparator_1_eq : 1'bz;  // Controlled_Buffer controlled_buffer_7
  not not_1 (not_1_out, AND);
  assign DATA_BUS_OUT = pull_resistor_2_node | DATA_BUS_IN;  // OR_Gate or_2, 8 bits wide
  Pull_Resistor pull_resistor_2 (.node(pull_resistor_2_node));
  assign pull_resistor_2_node = AND ? and_1_out : 8'bz;  // Controlled_Buffer controlled_buffer_8

  assign {FLAGS_OUT[7:5], FLAGS_OUT[0]} = {FLAGS_IN[7:5], FLAGS_IN[0]};
endmodule

module SHIFT (
  input  LSL,
  input  LSR,
  input  [7:0] Rd,
  input  ROL,
  input  ROR,
  input  ASR,
  input  [7:0] FLAGS_IN,
  input  FLAGS_ENABLE,
  input  [7:0] DATA_BUS_IN,
  output [7:0] FLAGS_OUT,
  output FLAGS_ENABLE_2,
  output [7:0] DATA_BUS_OUT
);

  wire comparator_1_eq, not_1_out, not_2_out, not_3_out, or_2_out, or_4_out, xor_1_out, xor_2_out;
  wire [6:0] controlled_buffer_1_out, controlled_buffer_3_out, controlled_buffer_6_out;
  wire [7:0] pull_resistor_1_node;
  wire [7:1] controlled_buffer_2_out, controlled_buffer_4_out, controlled_buffer_5_out;

  assign {FLAGS_OUT[0], controlled_buffer_1_out[6:5], FLAGS_OUT[5], controlled_buffer_1_out[3:0]} = LSL ? Rd : 8'bz;  // Controlled_Buffer controlled_buffer_1
  assign {controlled_buffer_2_out, FLAGS_OUT[0]} = LSR ? Rd : 8'bz;  // Controlled_Buffer controlled_buffer_2
  assign {FLAGS_OUT[0], controlled_buffer_3_out[6:4], FLAGS_OUT[5], controlled_buffer_3_out[2:0]} = ROL ? Rd : 8'bz;  // Controlled_Buffer controlled_buffer_3
  assign {controlled_buffer_4_out, FLAGS_OUT[0]} = ROR ? Rd : 8'bz;  // Controlled_Buffer controlled_buffer_4
  assign {controlled_buffer_5_out, FLAGS_OUT[0]} = ASR ? Rd : 8'bz;  // Controlled_Buffer controlled_buffer_5
  assign {FLAGS_OUT[2], controlled_buffer_6_out} = LSL ? {controlled_buffer_1_out[6:5], FLAGS_OUT[5], controlled_buffer_1_out[3:0], 1'b0} : 8'bz;  // Controlled_Buffer controlled_buffer_6
  assign {FLAGS_OUT[2], controlled_buffer_6_out} = LSR ? {1'b0, controlled_buffer_2_out} : 8'bz;  // Controlled_Buffer controlled_buffer_7
  assign {FLAGS_OUT[2], controlled_buffer_6_out} = ROL ? {controlled_buffer_3_out[6:4], FLAGS_OUT[5], controlled_buffer_3_out[2:0], FLAGS_IN[0]} : 8'bz;  // Controlled_Buffer controlled_buffer_8
  assign {FLAGS_OUT[2], controlled_buffer_6_out} = ROR ? {FLAGS_IN[0], controlled_buffer_4_out} : 8'bz;  // Controlled_Buffer controlled_buffer_9
  assign {FLAGS_OUT[2], controlled_buffer_6_out} = ASR ? {controlled_buffer_5_out[7], 1'b0, controlled_buffer_5_out[6:1]} : 8'bz;  // Controlled_Buffer controlled_buffer_10
  Comparator comparator_1 (
    .a({FLAGS_OUT[2], controlled_buffer_6_out}), .b({8{1'b0}}), .eq(comparator_1_eq));  // open: gt, lt
  assign FLAGS_OUT[3] = or_4_out ? xor_1_out : 1'bz;  // Controlled_Buffer controlled_buffer_11
  xor xor_1 (xor_1_out, FLAGS_OUT[0], FLAGS_OUT[2]);
  xor xor_2 (xor_2_out, FLAGS_OUT[2], FLAGS_OUT[3]);
  assign FLAGS_OUT[4] = or_4_out ? xor_2_out : 1'bz;  // Controlled_Buffer controlled_buffer_12
  assign FLAGS_OUT[1] = or_4_out ? comparator_1_eq : 1'bz;  // Controlled_Buffer controlled_buffer_13
  assign FLAGS_OUT[2] = LSR ? not_2_out : 1'bz;  // Controlled_Buffer controlled_buffer_14
  assign FLAGS_OUT[5] = not_1_out ? FLAGS_IN[5] : 1'bz;  // Controlled_Buffer controlled_buffer_15
  not not_1 (not_1_out, or_2_out);
  assign FLAGS_OUT[3] = not_3_out ? FLAGS_IN[3] : 1'bz;  // Controlled_Buffer controlled_buffer_16
  assign FLAGS_OUT[1] = not_3_out ? FLAGS_IN[1] : 1'bz;  // Controlled_Buffer controlled_buffer_17
  assign FLAGS_OUT[4] = not_3_out ? FLAGS_IN[4] : 1'bz;  // Controlled_Buffer controlled_buffer_18
  assign FLAGS_OUT[0] = not_3_out ? FLAGS_IN[0] : 1'bz;  // Controlled_Buffer controlled_buffer_19
  assign FLAGS_OUT[2] = not_3_out ? FLAGS_IN[2] : 1'bz;  // Controlled_Buffer controlled_buffer_20
  or or_1 (FLAGS_ENABLE_2, FLAGS_ENABLE, or_4_out);
  not not_2 (not_2_out, LSR);
  or or_2 (or_2_out, LSL, ROL);
  assign DATA_BUS_OUT = pull_resistor_1_node | DATA_BUS_IN;  // OR_Gate or_3, 8 bits wide
  Pull_Resistor pull_resistor_1 (.node(pull_resistor_1_node));
  assign pull_resistor_1_node = or_4_out ? {FLAGS_OUT[2], controlled_buffer_6_out} : 8'bz;  // Controlled_Buffer controlled_buffer_21
  not not_3 (not_3_out, or_4_out);
  or or_4 (or_4_out, LSL, LSR, ROL, ROR, ASR);

  assign FLAGS_OUT[7:6] = FLAGS_IN[7:6];
endmodule

// SUB
module SUBTRACTOR (
  input  [7:0] Rd,
  input  [7:0] Rr,
  input  SUB,
  input  SBC,
  input  [7:0] FLAGS_IN,
  input  FLAGS_ENABLE,
  input  [7:0] DATA_BUS_IN,
  output [7:0] FLAGS_OUT,
  output FLAGS_ENABLE_2,
  output [7:0] DATA_BUS_OUT
);

  wire and_1_out, and_2_out, comparator_1_eq, controlled_buffer_7_out, not_4_out, or_1_out, or_4_out,
       subtractor_1_bout, subtractor_2_bout, xor_1_out;
  wire [3:0] not_1_out, not_3_out;
  wire [7:0] not_2_out, pull_resistor_1_node, subtractor_1_out;

  assign not_1_out = ~Rr[7:4];  // NOT_Gate not_1, 4 bits wide
  assign not_2_out = ~subtractor_1_out;  // NOT_Gate not_2, 8 bits wide
  and and_1 (and_1_out, Rd[7], not_1_out[3], not_2_out[7]);
  or or_1 (or_1_out, and_1_out, and_2_out);
  assign not_3_out = ~Rd[7:4];  // NOT_Gate not_3, 4 bits wide
  and and_2 (and_2_out, not_3_out[3], Rr[7], subtractor_1_out[7]);
  Subtractor #(.width(4)) subtractor_1 (
    .a(Rd[3:0]), .b(Rr[3:0]), .out(subtractor_1_out[3:0]), .bin(controlled_buffer_7_out),
    .bout(subtractor_1_bout));
  Subtractor #(.width(4)) subtractor_2 (
    .a(Rd[7:4]), .b(Rr[7:4]), .out(subtractor_1_out[7:4]), .bin(subtractor_1_bout), .bout(subtractor_2_bout));
  assign FLAGS_OUT[0] = or_4_out ? subtractor_2_bout : 1'bz;  // Controlled_Buffer controlled_buffer_1
  assign FLAGS_OUT[1] = or_4_out ? comparator_1_eq : 1'bz;  // Controlled_Buffer controlled_buffer_2
  assign FLAGS_OUT[2] = or_4_out ? subtractor_1_out[7] : 1'bz;  // Controlled_Buffer controlled_buffer_3
  assign FLAGS_OUT[3] = or_4_out ? or_1_out : 1'bz;  // Controlled_Buffer controlled_buffer_4
  assign FLAGS_OUT[4] = or_4_out ? xor_1_out : 1'bz;  // Controlled_Buffer controlled_buffer_5
  xor xor_1 (xor_1_out, FLAGS_OUT[3], FLAGS_OUT[2]);
  assign FLAGS_OUT[5] = or_4_out ? subtractor_1_bout : 1'bz;  // Controlled_Buffer controlled_buffer_6
  assign controlled_buffer_7_out = SBC ? FLAGS_IN[0] : 1'bz;  // Controlled_Buffer controlled_buffer_7
  Comparator comparator_1 (.a(subtractor_1_out), .b({8{1'b0}}), .eq(comparator_1_eq));  // open: gt, lt
  assign FLAGS_OUT[1] = not_4_out ? FLAGS_IN[1] : 1'bz;  // Controlled_Buffer controlled_buffer_8
  assign FLAGS_OUT[0] = not_4_out ? FLAGS_IN[0] : 1'bz;  // Controlled_Buffer controlled_buffer_9
  assign FLAGS_OUT[4] = not_4_out ? FLAGS_IN[4] : 1'bz;  // Controlled_Buffer controlled_buffer_10
  assign FLAGS_OUT[2] = not_4_out ? FLAGS_IN[2] : 1'bz;  // Controlled_Buffer controlled_buffer_11
  assign FLAGS_OUT[3] = not_4_out ? FLAGS_IN[3] : 1'bz;  // Controlled_Buffer controlled_buffer_12
  assign FLAGS_OUT[5] = not_4_out ? FLAGS_IN[5] : 1'bz;  // Controlled_Buffer controlled_buffer_13
  or or_2 (FLAGS_ENABLE_2, FLAGS_ENABLE, or_4_out);
  not not_4 (not_4_out, or_4_out);
  assign DATA_BUS_OUT = pull_resistor_1_node | DATA_BUS_IN;  // OR_Gate or_3, 8 bits wide
  Pull_Resistor pull_resistor_1 (.node(pull_resistor_1_node));
  assign pull_resistor_1_node = or_4_out ? subtractor_1_out : 8'bz;  // Controlled_Buffer controlled_buffer_14
  or or_4 (or_4_out, SBC, SUB);

  assign FLAGS_OUT[7:6] = FLAGS_IN[7:6];
endmodule

module OR (
  input  [7:0] Rd,
  input  OR,
  input  [7:0] Rr,
  input  [7:0] FLAGS_IN,
  input  FLAGS_ENABLE,
  input  [7:0] DATA_BUS_IN,
  output [7:0] FLAGS_OUT,
  output FLAGS_ENABLE_2,
  output [7:0] DATA_BUS_OUT
);

  wire comparator_1_eq, not_1_out, xor_1_out;
  wire [7:0] or_1_out, pull_resistor_2_node;

  assign or_1_out = Rd | Rr;  // OR_Gate or_1, 8 bits wide
  assign FLAGS_OUT[2] = OR ? or_1_out[7] : 1'bz;  // Controlled_Buffer controlled_buffer_1
  assign FLAGS_OUT[4] = OR ? xor_1_out : 1'bz;  // Controlled_Buffer controlled_buffer_2
  xor xor_1 (xor_1_out, or_1_out[7], FLAGS_OUT[3]);
  assign FLAGS_OUT[4] = not_1_out ? FLAGS_IN[4] : 1'bz;  // Controlled_Buffer controlled_buffer_3
  Comparator comparator_1 (.a(or_1_out), .b({8{1'b0}}), .eq(comparator_1_eq));  // open: gt, lt
  Pull_Resistor pull_resistor_1 (.node(FLAGS_OUT[3]));
  assign FLAGS_OUT[3] = not_1_out ? FLAGS_IN[3] : 1'bz;  // Controlled_Buffer controlled_buffer_4
  assign FLAGS_OUT[2] = not_1_out ? FLAGS_IN[2] : 1'bz;  // Controlled_Buffer controlled_buffer_5
  assign FLAGS_OUT[1] = not_1_out ? FLAGS_IN[1] : 1'bz;  // Controlled_Buffer controlled_buffer_6
  or or_2 (FLAGS_ENABLE_2, FLAGS_ENABLE, OR);
  assign FLAGS_OUT[1] = OR ? comparator_1_eq : 1'bz;  // Controlled_Buffer controlled_buffer_7
  not not_1 (not_1_out, OR);
  assign DATA_BUS_OUT = pull_resistor_2_node | DATA_BUS_IN;  // OR_Gate or_3, 8 bits wide
  Pull_Resistor pull_resistor_2 (.node(pull_resistor_2_node));
  assign pull_resistor_2_node = OR ? or_1_out : 8'bz;  // Controlled_Buffer controlled_buffer_8

  assign {FLAGS_OUT[7:5], FLAGS_OUT[0]} = {FLAGS_IN[7:5], FLAGS_IN[0]};
endmodule

module EOR (
  input  [7:0] Rd,
  input  EOR,
  input  [7:0] Rr,
  input  [7:0] FLAGS_IN,
  input  FLAGS_ENABLE,
  input  [7:0] DATA_BUS_IN,
  output [7:0] FLAGS_OUT,
  output FLAGS_ENABLE_2,
  output [7:0] DATA_BUS_OUT
);

  wire comparator_1_eq, not_1_out, xor_2_out;
  wire [7:0] pull_resistor_2_node, xor_1_out;

  assign xor_1_out = Rd ^ Rr;  // XOR_Gate xor_1, 8 bits wide
  assign FLAGS_OUT[2] = EOR ? xor_1_out[7] : 1'bz;  // Controlled_Buffer controlled_buffer_1
  xor xor_2 (xor_2_out, xor_1_out[7], FLAGS_OUT[3]);
  assign FLAGS_OUT[4] = EOR ? xor_2_out : 1'bz;  // Controlled_Buffer controlled_buffer_2
  assign FLAGS_OUT[4] = not_1_out ? FLAGS_IN[4] : 1'bz;  // Controlled_Buffer controlled_buffer_3
  Comparator comparator_1 (.a(xor_1_out), .b({8{1'b0}}), .eq(comparator_1_eq));  // open: gt, lt
  Pull_Resistor pull_resistor_1 (.node(FLAGS_OUT[3]));
  assign FLAGS_OUT[3] = not_1_out ? FLAGS_IN[3] : 1'bz;  // Controlled_Buffer controlled_buffer_4
  assign FLAGS_OUT[1] = not_1_out ? FLAGS_IN[1] : 1'bz;  // Controlled_Buffer controlled_buffer_5
  assign FLAGS_OUT[2] = not_1_out ? FLAGS_IN[2] : 1'bz;  // Controlled_Buffer controlled_buffer_6
  or or_1 (FLAGS_ENABLE_2, FLAGS_ENABLE, EOR);
  assign FLAGS_OUT[1] = EOR ? comparator_1_eq : 1'bz;  // Controlled_Buffer controlled_buffer_7
  not not_1 (not_1_out, EOR);
  assign DATA_BUS_OUT = pull_resistor_2_node | DATA_BUS_IN;  // OR_Gate or_2, 8 bits wide
  Pull_Resistor pull_resistor_2 (.node(pull_resistor_2_node));
  assign pull_resistor_2_node = EOR ? xor_1_out : 8'bz;  // Controlled_Buffer controlled_buffer_8

  assign {FLAGS_OUT[7:5], FLAGS_OUT[0]} = {FLAGS_IN[7:5], FLAGS_IN[0]};
endmodule

module COM (
  input  [7:0] Rd,
  input  COM,
  input  [7:0] FLAGS_IN,
  input  FLAGS_ENABLE,
  input  [7:0] DATA_BUS_IN,
  output [7:0] FLAGS_OUT,
  output FLAGS_ENABLE_2,
  output [7:0] DATA_BUS_OUT
);

  wire comparator_1_eq, not_1_out, xor_1_out;
  wire [7:0] pull_resistor_3_node, subtractor_1_out;

  Subtractor subtractor_1 (.a({8{1'b1}}), .b(Rd), .out(subtractor_1_out));  // open: bin, bout
  assign FLAGS_OUT[2] = COM ? subtractor_1_out[7] : 1'bz;  // Controlled_Buffer controlled_buffer_1
  assign FLAGS_OUT[4] = COM ? xor_1_out : 1'bz;  // Controlled_Buffer controlled_buffer_2
  xor xor_1 (xor_1_out, subtractor_1_out[7], FLAGS_OUT[3]);
  assign FLAGS_OUT[4] = not_1_out ? FLAGS_IN[4] : 1'bz;  // Controlled_Buffer controlled_buffer_3
  Comparator comparator_1 (.a(subtractor_1_out), .b({8{1'b0}}), .eq(comparator_1_eq));  // open: gt, lt
  Pull_Resistor pull_resistor_1 (.node(FLAGS_OUT[0]));
  Pull_Resistor pull_resistor_2 (.node(FLAGS_OUT[3]));
  assign FLAGS_OUT[0] = not_1_out ? FLAGS_IN[0] : 1'bz;  // Controlled_Buffer controlled_buffer_4
  assign FLAGS_OUT[1] = not_1_out ? FLAGS_IN[1] : 1'bz;  // Controlled_Buffer controlled_buffer_5
  assign FLAGS_OUT[2] = not_1_out ? FLAGS_IN[2] : 1'bz;  // Controlled_Buffer controlled_buffer_6
  assign FLAGS_OUT[3] = not_1_out ? FLAGS_IN[3] : 1'bz;  // Controlled_Buffer controlled_buffer_7
  or or_1 (FLAGS_ENABLE_2, FLAGS_ENABLE, COM);
  assign FLAGS_OUT[1] = COM ? comparator_1_eq : 1'bz;  // Controlled_Buffer controlled_buffer_8
  not not_1 (not_1_out, COM);
  assign DATA_BUS_OUT = pull_resistor_3_node | DATA_BUS_IN;  // OR_Gate or_2, 8 bits wide
  Pull_Resistor pull_resistor_3 (.node(pull_resistor_3_node));
  assign pull_resistor_3_node = COM ? subtractor_1_out : 8'bz;  // Controlled_Buffer controlled_buffer_9

  assign FLAGS_OUT[7:5] = FLAGS_IN[7:5];
endmodule

module NEG (
  input  [7:0] Rd,
  input  COM,
  input  [7:0] FLAGS_IN,
  input  FLAGS_ENABLE,
  input  [7:0] DATA_BUS_IN,
  output [7:0] FLAGS_OUT,
  output FLAGS_ENABLE_2,
  output [7:0] DATA_BUS_OUT
);

  wire comparator_1_eq, comparator_2_eq, not_1_out, not_2_out, or_1_out, xor_1_out;
  wire [7:0] pull_resistor_1_node, subtractor_1_out;

  Subtractor subtractor_1 (.a({8{1'b0}}), .b(Rd), .out(subtractor_1_out));  // open: bin, bout
  assign FLAGS_OUT[2] = COM ? subtractor_1_out[7] : 1'bz;  // Controlled_Buffer controlled_buffer_1
  assign FLAGS_OUT[4] = COM ? xor_1_out : 1'bz;  // Controlled_Buffer controlled_buffer_2
  xor xor_1 (xor_1_out, subtractor_1_out[7], FLAGS_OUT[3]);
  or or_1 (or_1_out, subtractor_1_out[3], Rd[3]);
  assign FLAGS_OUT[5] = COM ? or_1_out : 1'bz;  // Controlled_Buffer controlled_buffer_3
  assign FLAGS_OUT[3] = COM ? comparator_1_eq : 1'bz;  // Controlled_Buffer controlled_buffer_4
  Comparator comparator_1 (.a(subtractor_1_out), .b(8'h80), .eq(comparator_1_eq));  // open: gt, lt
  Comparator comparator_2 (.a(subtractor_1_out), .b({8{1'b0}}), .eq(comparator_2_eq));  // open: gt, lt
  assign FLAGS_OUT[1] = not_2_out ? FLAGS_IN[1] : 1'bz;  // Controlled_Buffer controlled_buffer_5
  assign FLAGS_OUT[4] = not_2_out ? FLAGS_IN[4] : 1'bz;  // Controlled_Buffer controlled_buffer_6
  assign FLAGS_OUT[2] = not_2_out ? FLAGS_IN[2] : 1'bz;  // Controlled_Buffer controlled_buffer_7
  assign FLAGS_OUT[0] = not_2_out ? FLAGS_IN[0] : 1'bz;  // Controlled_Buffer controlled_buffer_8
  assign FLAGS_OUT[5] = not_2_out ? FLAGS_IN[5] : 1'bz;  // Controlled_Buffer controlled_buffer_9
  assign FLAGS_OUT[3] = not_2_out ? FLAGS_IN[3] : 1'bz;  // Controlled_Buffer controlled_buffer_10
  or or_2 (FLAGS_ENABLE_2, FLAGS_ENABLE, COM);
  assign FLAGS_OUT[1] = COM ? comparator_2_eq : 1'bz;  // Controlled_Buffer controlled_buffer_11
  not not_1 (not_1_out, comparator_2_eq);
  assign FLAGS_OUT[0] = COM ? not_1_out : 1'bz;  // Controlled_Buffer controlled_buffer_12
  not not_2 (not_2_out, COM);
  assign DATA_BUS_OUT = pull_resistor_1_node | DATA_BUS_IN;  // OR_Gate or_3, 8 bits wide
  Pull_Resistor pull_resistor_1 (.node(pull_resistor_1_node));
  assign pull_resistor_1_node = COM ? subtractor_1_out : 8'bz;  // Controlled_Buffer controlled_buffer_13

  assign FLAGS_OUT[7:6] = FLAGS_IN[7:6];
endmodule

// Registers
module RegisterFile (
  input  [7:0] Rd_IN,
  input  WORD_EN,
  input  plus_1_Offset,
  input  [4:0] Rd,
  input  Rd_En,
  input  Rr_En,
  input  [4:0] Rr,
  output [15:0] Indirect_OUT,
  output [7:0] Rd_OUT,
  output [7:0] Rr_OUT
);

  wire clock_1_out, decoder_1_out0, decoder_1_out1, decoder_1_out2, decoder_1_out3, decoder_1_out4,
       decoder_1_out5, decoder_1_out6, decoder_1_out7, decoder_1_out8, decoder_1_out9, decoder_1_out10,
       decoder_1_out11, decoder_1_out12, decoder_1_out13, decoder_1_out14, decoder_1_out15, decoder_1_out16,
       decoder_1_out17, decoder_1_out18, decoder_1_out19, decoder_1_out20, decoder_1_out21, decoder_1_out22,
       decoder_1_out23, decoder_1_out24, decoder_1_out25, decoder_1_out26, decoder_1_out27, decoder_1_out28,
       decoder_1_out29, decoder_1_out30, decoder_1_out31, decoder_2_out0, decoder_2_out1, decoder_2_out2,
       decoder_2_out3, decoder_2_out4, decoder_2_out5, decoder_2_out6, decoder_2_out7, decoder_2_out8,
       decoder_2_out9, decoder_2_out10, decoder_2_out11, decoder_2_out12, decoder_2_out13, decoder_2_out14,
       decoder_2_out15, decoder_2_out16, decoder_2_out17, decoder_2_out18, decoder_2_out19, decoder_2_out20,
       decoder_2_out21, decoder_2_out22, decoder_2_out23, decoder_2_out24, decoder_2_out25, decoder_2_out26,
       decoder_2_out27, decoder_2_out28, decoder_2_out29, decoder_2_out30, decoder_2_out31, not_1_out,
       or_2_out, or_4_out;
  wire [4:0] controlled_buffer_2_out, controlled_buffer_3_out, or_1_out, or_3_out;
  wire [7:0] controlled_buffer_6_out, controlled_buffer_9_out, controlled_buffer_12_out,
       controlled_buffer_15_out, controlled_buffer_18_out, controlled_buffer_21_out,
       controlled_buffer_24_out, controlled_buffer_27_out, controlled_buffer_29_out,
       controlled_buffer_30_out, controlled_buffer_31_out, controlled_buffer_32_out,
       controlled_buffer_33_out, controlled_buffer_34_out, controlled_buffer_35_out,
       controlled_buffer_36_out, controlled_buffer_38_out, controlled_buffer_41_out,
       controlled_buffer_44_out, controlled_buffer_47_out, controlled_buffer_50_out,
       controlled_buffer_53_out, controlled_buffer_56_out, controlled_buffer_59_out,
       controlled_buffer_78_out, controlled_buffer_81_out, controlled_buffer_84_out,
       controlled_buffer_87_out, controlled_buffer_90_out, controlled_buffer_93_out,
       controlled_buffer_96_out, controlled_buffer_99_out, register_1_q, register_2_q, register_3_q,
       register_4_q, register_5_q, register_6_q, register_7_q, register_8_q, register_9_q, register_10_q,
       register_11_q, register_12_q, register_13_q, register_14_q, register_15_q, register_16_q,
       register_17_q, register_18_q, register_19_q, register_20_q, register_21_q, register_22_q,
       register_23_q, register_24_q, register_25_q, register_26_q, register_27_q, register_28_q,
       register_29_q, register_30_q, register_31_q, register_32_q;

  assign or_1_out = controlled_buffer_3_out | Rr;  // OR_Gate or_1, 5 bits wide
  Decoder_part #(.select(5), .disabled(0)) decoder_1 (
    .out0(decoder_1_out0), .out1(decoder_1_out1), .out2(decoder_1_out2), .out3(decoder_1_out3),
    .out4(decoder_1_out4), .out5(decoder_1_out5), .out6(decoder_1_out6), .out7(decoder_1_out7),
    .out8(decoder_1_out8), .out9(decoder_1_out9), .out10(decoder_1_out10), .out11(decoder_1_out11),
    .out12(decoder_1_out12), .out13(decoder_1_out13), .out14(decoder_1_out14), .out15(decoder_1_out15),
    .out16(decoder_1_out16), .out17(decoder_1_out17), .out18(decoder_1_out18), .out19(decoder_1_out19),
    .out20(decoder_1_out20), .out21(decoder_1_out21), .out22(decoder_1_out22), .out23(decoder_1_out23),
    .out24(decoder_1_out24), .out25(decoder_1_out25), .out26(decoder_1_out26), .out27(decoder_1_out27),
    .out28(decoder_1_out28), .out29(decoder_1_out29), .out30(decoder_1_out30), .out31(decoder_1_out31),
    .sel(or_1_out), .en(or_2_out));
  assign Indirect_OUT = WORD_EN ? {Rr_OUT, Rd_OUT} : 16'bz;  // Controlled_Buffer controlled_buffer_1
  Pull_Resistor pull_resistor_1 (.node(Indirect_OUT));
  // Probe on controlled_buffer_3_out
  or or_2 (or_2_out, WORD_EN, Rr_En);
  not not_1 (not_1_out, plus_1_Offset);
  assign or_3_out = 5'b00001 | Rd;  // OR_Gate or_3, 5 bits wide
  assign controlled_buffer_2_out = plus_1_Offset ? or_3_out : 5'bz;  // Controlled_Buffer controlled_buffer_2
  assign controlled_buffer_3_out = WORD_EN ? or_3_out : 5'bz;  // Controlled_Buffer controlled_buffer_3
  Pull_Resistor pull_resistor_2 (.node(controlled_buffer_3_out));
  or or_4 (or_4_out, Rd_En, WORD_EN);
  assign controlled_buffer_2_out = not_1_out ? Rd : 5'bz;  // Controlled_Buffer controlled_buffer_4
  Decoder_part #(.select(5), .disabled(0)) decoder_2 (
    .out0(decoder_2_out0), .out1(decoder_2_out1), .out2(decoder_2_out2), .out3(decoder_2_out3),
    .out4(decoder_2_out4), .out5(decoder_2_out5), .out6(decoder_2_out6), .out7(decoder_2_out7),
    .out8(decoder_2_out8), .out9(decoder_2_out9), .out10(decoder_2_out10), .out11(decoder_2_out11),
    .out12(decoder_2_out12), .out13(decoder_2_out13), .out14(decoder_2_out14), .out15(decoder_2_out15),
    .out16(decoder_2_out16), .out17(decoder_2_out17), .out18(decoder_2_out18), .out19(decoder_2_out19),
    .out20(decoder_2_out20), .out21(decoder_2_out21), .out22(decoder_2_out22), .out23(decoder_2_out23),
    .out24(decoder_2_out24), .out25(decoder_2_out25), .out26(decoder_2_out26), .out27(decoder_2_out27),
    .out28(decoder_2_out28), .out29(decoder_2_out29), .out30(decoder_2_out30), .out31(decoder_2_out31),
    .sel(controlled_buffer_2_out), .en(or_4_out));
  Pull_Resistor pull_resistor_3 (.node(Rd_OUT));
  Pull_Resistor pull_resistor_4 (.node(Rr_OUT));
  Clock clock_1 (.out(clock_1_out));
  assign Rr_OUT = decoder_1_out0 ? register_1_q : 8'bz;  // Controlled_Buffer controlled_buffer_5
  Register register_1 (
    .D(controlled_buffer_6_out), .en(decoder_2_out0), .Q(register_1_q), .clk(clock_1_out));  // open: clr
  assign controlled_buffer_6_out = decoder_2_out0 ? Rd_IN : 8'bz;  // Controlled_Buffer controlled_buffer_6
  assign Rd_OUT = decoder_2_out0 ? register_1_q : 8'bz;  // Controlled_Buffer controlled_buffer_7
  assign Rr_OUT = decoder_1_out4 ? register_2_q : 8'bz;  // Controlled_Buffer controlled_buffer_8
  Register register_2 (
    .D(controlled_buffer_9_out), .en(decoder_2_out4), .Q(register_2_q), .clk(clock_1_out));  // open: clr
  assign controlled_buffer_9_out = decoder_2_out4 ? Rd_IN : 8'bz;  // Controlled_Buffer controlled_buffer_9
  assign Rd_OUT = decoder_2_out4 ? register_2_q : 8'bz;  // Controlled_Buffer controlled_buffer_10
  assign Rr_OUT = decoder_1_out8 ? register_3_q : 8'bz;  // Controlled_Buffer controlled_buffer_11
  assign controlled_buffer_12_out = decoder_2_out8 ? Rd_IN : 8'bz;  // Controlled_Buffer controlled_buffer_12
  Register register_3 (
    .D(controlled_buffer_12_out), .en(decoder_2_out8), .Q(register_3_q), .clk(clock_1_out));  // open: clr
  assign Rd_OUT = decoder_2_out8 ? register_3_q : 8'bz;  // Controlled_Buffer controlled_buffer_13
  assign Rr_OUT = decoder_1_out12 ? register_4_q : 8'bz;  // Controlled_Buffer controlled_buffer_14
  Register register_4 (
    .D(controlled_buffer_15_out), .en(decoder_2_out12), .Q(register_4_q), .clk(clock_1_out));  // open: clr
  assign controlled_buffer_15_out = decoder_2_out12 ? Rd_IN : 8'bz;  // Controlled_Buffer controlled_buffer_15
  assign Rd_OUT = decoder_2_out12 ? register_4_q : 8'bz;  // Controlled_Buffer controlled_buffer_16
  assign Rr_OUT = decoder_1_out16 ? register_5_q : 8'bz;  // Controlled_Buffer controlled_buffer_17
  assign controlled_buffer_18_out = decoder_2_out16 ? Rd_IN : 8'bz;  // Controlled_Buffer controlled_buffer_18
  Register register_5 (
    .D(controlled_buffer_18_out), .en(decoder_2_out16), .Q(register_5_q), .clk(clock_1_out));  // open: clr
  assign Rd_OUT = decoder_2_out16 ? register_5_q : 8'bz;  // Controlled_Buffer controlled_buffer_19
  assign Rr_OUT = decoder_1_out20 ? register_6_q : 8'bz;  // Controlled_Buffer controlled_buffer_20
  assign controlled_buffer_21_out = decoder_2_out20 ? Rd_IN : 8'bz;  // Controlled_Buffer controlled_buffer_21
  Register register_6 (
    .D(controlled_buffer_21_out), .en(decoder_2_out20), .Q(register_6_q), .clk(clock_1_out));  // open: clr
  assign Rd_OUT = decoder_2_out20 ? register_6_q : 8'bz;  // Controlled_Buffer controlled_buffer_22
  assign Rr_OUT = decoder_1_out24 ? register_7_q : 8'bz;  // Controlled_Buffer controlled_buffer_23
  assign controlled_buffer_24_out = decoder_2_out24 ? Rd_IN : 8'bz;  // Controlled_Buffer controlled_buffer_24
  Register register_7 (
    .D(controlled_buffer_24_out), .en(decoder_2_out24), .Q(register_7_q), .clk(clock_1_out));  // open: clr
  assign Rd_OUT = decoder_2_out24 ? register_7_q : 8'bz;  // Controlled_Buffer controlled_buffer_25
  assign Rr_OUT = decoder_1_out28 ? register_8_q : 8'bz;  // Controlled_Buffer controlled_buffer_26
  Register register_8 (
    .D(controlled_buffer_27_out), .en(decoder_2_out28), .Q(register_8_q), .clk(clock_1_out));  // open: clr
  assign controlled_buffer_27_out = decoder_2_out28 ? Rd_IN : 8'bz;  // Controlled_Buffer controlled_buffer_27
  assign Rd_OUT = decoder_2_out28 ? register_8_q : 8'bz;  // Controlled_Buffer controlled_buffer_28
  Register register_9 (
    .D(controlled_buffer_29_out), .en(decoder_2_out1), .Q(register_9_q), .clk(clock_1_out));  // open: clr
  assign controlled_buffer_29_out = decoder_2_out1 ? Rd_IN : 8'bz;  // Controlled_Buffer controlled_buffer_29
  Register register_10 (
    .D(controlled_buffer_30_out), .en(decoder_2_out5), .Q(register_10_q), .clk(clock_1_out));  // open: clr
  assign controlled_buffer_30_out = decoder_2_out5 ? Rd_IN : 8'bz;  // Controlled_Buffer controlled_buffer_30
  Register register_11 (
    .D(controlled_buffer_31_out), .en(decoder_2_out9), .Q(register_11_q), .clk(clock_1_out));  // open: clr
  assign controlled_buffer_31_out = decoder_2_out9 ? Rd_IN : 8'bz;  // Controlled_Buffer controlled_buffer_31
  assign controlled_buffer_32_out = decoder_2_out13 ? Rd_IN : 8'bz;  // Controlled_Buffer controlled_buffer_32
  Register register_12 (
    .D(controlled_buffer_32_out), .en(decoder_2_out13), .Q(register_12_q), .clk(clock_1_out));  // open: clr
  Register register_13 (
    .D(controlled_buffer_33_out), .en(decoder_2_out17), .Q(register_13_q), .clk(clock_1_out));  // open: clr
  assign controlled_buffer_33_out = decoder_2_out17 ? Rd_IN : 8'bz;  // Controlled_Buffer controlled_buffer_33
  Register register_14 (
    .D(controlled_buffer_34_out), .en(decoder_2_out21), .Q(register_14_q), .clk(clock_1_out));  // open: clr
  assign controlled_buffer_34_out = decoder_2_out21 ? Rd_IN : 8'bz;  // Controlled_Buffer controlled_buffer_34
  Register register_15 (
    .D(controlled_buffer_35_out), .en(decoder_2_out25), .Q(register_15_q), .clk(clock_1_out));  // open: clr
  assign controlled_buffer_35_out = decoder_2_out25 ? Rd_IN : 8'bz;  // Controlled_Buffer controlled_buffer_35
  Register register_16 (
    .D(controlled_buffer_36_out), .en(decoder_2_out29), .Q(register_16_q), .clk(clock_1_out));  // open: clr
  assign controlled_buffer_36_out = decoder_2_out29 ? Rd_IN : 8'bz;  // Controlled_Buffer controlled_buffer_36
  assign Rr_OUT = decoder_1_out1 ? register_9_q : 8'bz;  // Controlled_Buffer controlled_buffer_37
  assign controlled_buffer_38_out = decoder_2_out2 ? Rd_IN : 8'bz;  // Controlled_Buffer controlled_buffer_38
  assign Rd_OUT = decoder_2_out1 ? register_9_q : 8'bz;  // Controlled_Buffer controlled_buffer_39
  assign Rr_OUT = decoder_1_out5 ? register_10_q : 8'bz;  // Controlled_Buffer controlled_buffer_40
  assign controlled_buffer_41_out = decoder_2_out6 ? Rd_IN : 8'bz;  // Controlled_Buffer controlled_buffer_41
  assign Rd_OUT = decoder_2_out5 ? register_10_q : 8'bz;  // Controlled_Buffer controlled_buffer_42
  assign Rr_OUT = decoder_1_out9 ? register_11_q : 8'bz;  // Controlled_Buffer controlled_buffer_43
  assign controlled_buffer_44_out = decoder_2_out10 ? Rd_IN : 8'bz;  // Controlled_Buffer controlled_buffer_44
  assign Rd_OUT = decoder_2_out9 ? register_11_q : 8'bz;  // Controlled_Buffer controlled_buffer_45
  assign Rr_OUT = decoder_1_out13 ? register_12_q : 8'bz;  // Controlled_Buffer controlled_buffer_46
  assign controlled_buffer_47_out = decoder_2_out14 ? Rd_IN : 8'bz;  // Controlled_Buffer controlled_buffer_47
  assign Rd_OUT = decoder_2_out13 ? register_12_q : 8'bz;  // Controlled_Buffer controlled_buffer_48
  assign Rr_OUT = decoder_1_out17 ? register_13_q : 8'bz;  // Controlled_Buffer controlled_buffer_49
  assign controlled_buffer_50_out = decoder_2_out18 ? Rd_IN : 8'bz;  // Controlled_Buffer controlled_buffer_50
  assign Rd_OUT = decoder_2_out17 ? register_13_q : 8'bz;  // Controlled_Buffer controlled_buffer_51
  assign Rr_OUT = decoder_1_out21 ? register_14_q : 8'bz;  // Controlled_Buffer controlled_buffer_52
  assign controlled_buffer_53_out = decoder_2_out22 ? Rd_IN : 8'bz;  // Controlled_Buffer controlled_buffer_53
  assign Rd_OUT = decoder_2_out21 ? register_14_q : 8'bz;  // Controlled_Buffer controlled_buffer_54
  assign Rr_OUT = decoder_1_out25 ? register_15_q : 8'bz;  // Controlled_Buffer controlled_buffer_55
  assign controlled_buffer_56_out = decoder_2_out26 ? Rd_IN : 8'bz;  // Controlled_Buffer controlled_buffer_56
  assign Rd_OUT = decoder_2_out25 ? register_15_q : 8'bz;  // Controlled_Buffer controlled_buffer_57
  assign Rr_OUT = decoder_1_out29 ? register_16_q : 8'bz;  // Controlled_Buffer controlled_buffer_58
  assign controlled_buffer_59_out = decoder_2_out30 ? Rd_IN : 8'bz;  // Controlled_Buffer controlled_buffer_59
  assign Rd_OUT = decoder_2_out29 ? register_16_q : 8'bz;  // Controlled_Buffer controlled_buffer_60
  assign Rr_OUT = decoder_1_out2 ? register_17_q : 8'bz;  // Controlled_Buffer controlled_buffer_61
  Register register_17 (
    .D(controlled_buffer_38_out), .en(decoder_2_out2), .Q(register_17_q), .clk(clock_1_out));  // open: clr
  assign Rd_OUT = decoder_2_out2 ? register_17_q : 8'bz;  // Controlled_Buffer controlled_buffer_62
  assign Rr_OUT = decoder_1_out6 ? register_18_q : 8'bz;  // Controlled_Buffer controlled_buffer_63
  Register register_18 (
    .D(controlled_buffer_41_out), .en(decoder_2_out6), .Q(register_18_q), .clk(clock_1_out));  // open: clr
  assign Rd_OUT = decoder_2_out6 ? register_18_q : 8'bz;  // Controlled_Buffer controlled_buffer_64
  assign Rr_OUT = decoder_1_out10 ? register_19_q : 8'bz;  // Controlled_Buffer controlled_buffer_65
  Register register_19 (
    .D(controlled_buffer_44_out), .en(decoder_2_out10), .Q(register_19_q), .clk(clock_1_out));  // open: clr
  assign Rd_OUT = decoder_2_out10 ? register_19_q : 8'bz;  // Controlled_Buffer controlled_buffer_66
  assign Rr_OUT = decoder_1_out14 ? register_20_q : 8'bz;  // Controlled_Buffer controlled_buffer_67
  Register register_20 (
    .D(controlled_buffer_47_out), .en(decoder_2_out14), .Q(register_20_q), .clk(clock_1_out));  // open: clr
  assign Rd_OUT = decoder_2_out14 ? register_20_q : 8'bz;  // Controlled_Buffer controlled_buffer_68
  assign Rr_OUT = decoder_1_out18 ? register_21_q : 8'bz;  // Controlled_Buffer controlled_buffer_69
  Register register_21 (
    .D(controlled_buffer_50_out), .en(decoder_2_out18), .Q(register_21_q), .clk(clock_1_out));  // open: clr
  assign Rd_OUT = decoder_2_out18 ? register_21_q : 8'bz;  // Controlled_Buffer controlled_buffer_70
  assign Rr_OUT = decoder_1_out22 ? register_22_q : 8'bz;  // Controlled_Buffer controlled_buffer_71
  Register register_22 (
    .D(controlled_buffer_53_out), .en(decoder_2_out22), .Q(register_22_q), .clk(clock_1_out));  // open: clr
  assign Rd_OUT = decoder_2_out22 ? register_22_q : 8'bz;  // Controlled_Buffer controlled_buffer_72
  assign Rr_OUT = decoder_1_out26 ? register_23_q : 8'bz;  // Controlled_Buffer controlled_buffer_73
  Register register_23 (
    .D(controlled_buffer_56_out), .en(decoder_2_out26), .Q(register_23_q), .clk(clock_1_out));  // open: clr
  assign Rd_OUT = decoder_2_out26 ? register_23_q : 8'bz;  // Controlled_Buffer controlled_buffer_74
  assign Rr_OUT = decoder_1_out30 ? register_24_q : 8'bz;  // Controlled_Buffer controlled_buffer_75
  Register register_24 (
    .D(controlled_buffer_59_out), .en(decoder_2_out30), .Q(register_24_q), .clk(clock_1_out));  // open: clr
  assign Rd_OUT = decoder_2_out30 ? register_24_q : 8'bz;  // Controlled_Buffer controlled_buffer_76
  assign Rr_OUT = decoder_1_out3 ? register_25_q : 8'bz;  // Controlled_Buffer controlled_buffer_77
  Register register_25 (
    .D(controlled_buffer_78_out), .en(decoder_2_out3), .Q(register_25_q), .clk(clock_1_out));  // open: clr
  assign controlled_buffer_78_out = decoder_2_out3 ? Rd_IN : 8'bz;  // Controlled_Buffer controlled_buffer_78
  assign Rd_OUT = decoder_2_out3 ? register_25_q : 8'bz;  // Controlled_Buffer controlled_buffer_79
  assign Rr_OUT = decoder_1_out7 ? register_26_q : 8'bz;  // Controlled_Buffer controlled_buffer_80
  Register register_26 (
    .D(controlled_buffer_81_out), .en(decoder_2_out7), .Q(register_26_q), .clk(clock_1_out));  // open: clr
  assign controlled_buffer_81_out = decoder_2_out7 ? Rd_IN : 8'bz;  // Controlled_Buffer controlled_buffer_81
  assign Rd_OUT = decoder_2_out7 ? register_26_q : 8'bz;  // Controlled_Buffer controlled_buffer_82
  assign Rr_OUT = decoder_1_out11 ? register_27_q : 8'bz;  // Controlled_Buffer controlled_buffer_83
  assign controlled_buffer_84_out = decoder_2_out11 ? Rd_IN : 8'bz;  // Controlled_Buffer controlled_buffer_84
  Register register_27 (
    .D(controlled_buffer_84_out), .en(decoder_2_out11), .Q(register_27_q), .clk(clock_1_out));  // open: clr
  assign Rd_OUT = decoder_2_out11 ? register_27_q : 8'bz;  // Controlled_Buffer controlled_buffer_85
  assign Rr_OUT = decoder_1_out15 ? register_28_q : 8'bz;  // Controlled_Buffer controlled_buffer_86
  assign controlled_buffer_87_out = decoder_2_out15 ? Rd_IN : 8'bz;  // Controlled_Buffer controlled_buffer_87
  Register register_28 (
    .D(controlled_buffer_87_out), .en(decoder_2_out15), .Q(register_28_q), .clk(clock_1_out));  // open: clr
  assign Rd_OUT = decoder_2_out15 ? register_28_q : 8'bz;  // Controlled_Buffer controlled_buffer_88
  assign Rr_OUT = decoder_1_out19 ? register_29_q : 8'bz;  // Controlled_Buffer controlled_buffer_89
  Register register_29 (
    .D(controlled_buffer_90_out), .en(decoder_2_out19), .Q(register_29_q), .clk(clock_1_out));  // open: clr
  assign controlled_buffer_90_out = decoder_2_out19 ? Rd_IN : 8'bz;  // Controlled_Buffer controlled_buffer_90
  assign Rd_OUT = decoder_2_out19 ? register_29_q : 8'bz;  // Controlled_Buffer controlled_buffer_91
  assign Rr_OUT = decoder_1_out23 ? register_30_q : 8'bz;  // Controlled_Buffer controlled_buffer_92
  assign controlled_buffer_93_out = decoder_2_out23 ? Rd_IN : 8'bz;  // Controlled_Buffer controlled_buffer_93
  Register register_30 (
    .D(controlled_buffer_93_out), .en(decoder_2_out23), .Q(register_30_q), .clk(clock_1_out));  // open: clr
  assign Rd_OUT = decoder_2_out23 ? register_30_q : 8'bz;  // Controlled_Buffer controlled_buffer_94
  assign Rr_OUT = decoder_1_out27 ? register_31_q : 8'bz;  // Controlled_Buffer controlled_buffer_95
  assign controlled_buffer_96_out = decoder_2_out27 ? Rd_IN : 8'bz;  // Controlled_Buffer controlled_buffer_96
  Register register_31 (
    .D(controlled_buffer_96_out), .en(decoder_2_out27), .Q(register_31_q), .clk(clock_1_out));  // open: clr
  assign Rd_OUT = decoder_2_out27 ? register_31_q : 8'bz;  // Controlled_Buffer controlled_buffer_97
  assign Rr_OUT = decoder_1_out31 ? register_32_q : 8'bz;  // Controlled_Buffer controlled_buffer_98
  assign controlled_buffer_99_out = decoder_2_out31 ? Rd_IN : 8'bz;  // Controlled_Buffer controlled_buffer_99
  Register register_32 (
    .D(controlled_buffer_99_out), .en(decoder_2_out31), .Q(register_32_q), .clk(clock_1_out));  // open: clr
  assign Rd_OUT = decoder_2_out31 ? register_32_q : 8'bz;  // Controlled_Buffer controlled_buffer_100
endmodule

module FLASH (
  input  [15:0] PC_IN,
  input  [15:0] Indirect_IN,
  output [15:0] DATA_OUT
);

  wire clock_1_out;

  Clock clock_1 (.out(clock_1_out));
  RAM_part #(.addrWidth(16), .dataWidth(16), .bus("separate")) ram_1 (
    .addr(PC_IN), .din(Indirect_IN), .data(DATA_OUT), .str(1'b0), .clk(clock_1_out));  // open: sel, ld, clr
endmodule

// PC
module ProgCounter (
  input  [7:0] Data_IN,
  input  [2:0] Bit_to_check,
  input  BRBC,
  input  BRBS,
  input  [15:0] Indirect_IN,
  input  [15:0] Relative_Offset,
  input  [31:0] CONTROL,
  output [15:0] PC_2_OUT,
  output [15:0] PC_OUT
);

  wire clock_1_out, comparator_1_eq, not_1_out, or_2_out, or_3_out, pull_resistor_4_node;
  wire [7:0] and_1_out, shifter_1_out;
  wire [15:0] adder_2_out, adder_3_out, controlled_buffer_1_out, or_1_out, pull_resistor_2_node,
       pull_resistor_3_node;

  Adder #(.width(16)) adder_1 (.a(16'h1), .b(PC_OUT), .out(PC_2_OUT));  // open: cin, cout
  assign controlled_buffer_1_out = CONTROL[25] ? {PC_OUT[15:8], Data_IN} : 16'bz;  // Controlled_Buffer controlled_buffer_1
  Pull_Resistor pull_resistor_1 (.node(controlled_buffer_1_out));
  assign or_1_out = controlled_buffer_1_out | pull_resistor_3_node | pull_resistor_2_node;  // OR_Gate or_1, 16 bits wide
  or or_2 (or_2_out, CONTROL[25], or_3_out, CONTROL[29], CONTROL[26]);
  Pull_Resistor pull_resistor_2 (.node(pull_resistor_2_node));
  assign pull_resistor_2_node = CONTROL[26] ? {Data_IN, PC_OUT[7:0]} : 16'bz;  // Controlled_Buffer controlled_buffer_2
  Counter #(.width(16), .max('hffff), .trigger("falling")) counter_1 (
    .load(or_2_out), .D(or_1_out), .count(CONTROL[27]), .Q(PC_OUT), .clk(clock_1_out), .clr(CONTROL[28]));  // open: carry
  Clock clock_1 (.out(clock_1_out));
  Shifter shifter_1 (.in(8'h1), .\dist (Bit_to_check), .out(shifter_1_out));
  Pull_Resistor pull_resistor_3 (.node(pull_resistor_3_node));
  assign pull_resistor_3_node = CONTROL[29] ? Indirect_IN : 16'bz;  // Controlled_Buffer controlled_buffer_3
  assign and_1_out = shifter_1_out & Data_IN;  // AND_Gate and_1, 8 bits wide
  Comparator comparator_1 (.a(and_1_out), .b({8{1'b0}}), .eq(comparator_1_eq));  // open: gt, lt
  Pull_Resistor pull_resistor_4 (.node(pull_resistor_4_node));
  assign pull_resistor_3_node = or_3_out ? adder_3_out : 16'bz;  // Controlled_Buffer controlled_buffer_4
  or or_3 (or_3_out, pull_resistor_4_node, CONTROL[30]);
  assign pull_resistor_4_node = BRBS ? not_1_out : 1'bz;  // Controlled_Buffer controlled_buffer_5
  assign pull_resistor_4_node = BRBC ? comparator_1_eq : 1'bz;  // Controlled_Buffer controlled_buffer_6
  Adder #(.width(16)) adder_2 (.a(PC_OUT), .b(16'h1), .out(adder_2_out));  // open: cin, cout
  not not_1 (not_1_out, comparator_1_eq);
  Adder #(.width(16)) adder_3 (.a(Relative_Offset), .b(adder_2_out), .out(adder_3_out));  // open: cin, cout

  // Notes on the sheet:
  //   LD LO
  //   PC Enable
  //   LD HI
  //   Reset
  //   Load
  //   Add Offset
endmodule

// INST
module Instr_Reg (
  input  [15:0] in_1,
  input  [31:0] in_2,
  output [15:0] Params_OUT,
  output [15:0] out_4,
  output [2:0] Bits_OUT,
  output [7:0] Immediate_OUT
);

  wire clock_1_out, decoder_1_out0, decoder_1_out1, decoder_1_out2, decoder_1_out3, or_1_out;
  wire [4:0] adder_1_out, bit_extender_1_out, controlled_buffer_1_out, controlled_buffer_3_out,
       controlled_buffer_4_out;
  wire [7:0] bit_extender_5_out;
  wire [15:0] bit_extender_2_out, bit_extender_3_out, bit_extender_4_out;

  Clock clock_1 (.out(clock_1_out));
  Register #(.width(16), .trigger("high")) register_1 (.D(in_1), .Q(out_4), .clk(clock_1_out));  // open: en, clr
  assign bit_extender_1_out = {{1{1'b0}}, out_4[7:4]};  // Bit_Extender bit_extender_1
  assign controlled_buffer_1_out = in_2[9] ? out_4[8:4] : 5'bz;  // Controlled_Buffer controlled_buffer_1
  assign controlled_buffer_1_out = in_2[10] ? adder_1_out : 5'bz;  // Controlled_Buffer controlled_buffer_2
  Adder #(.width(5)) adder_1 (.a(bit_extender_1_out), .b(5'b10000), .out(adder_1_out));  // open: cin, cout
  assign controlled_buffer_3_out = in_2[8] ? {out_4[9], out_4[3:0]} : 5'bz;  // Controlled_Buffer controlled_buffer_3
  Decoder_part #(.select(2), .disabled(0)) decoder_1 (
    .out0(decoder_1_out0), .out1(decoder_1_out1), .out2(decoder_1_out2), .out3(decoder_1_out3),
    .sel(out_4[5:4]), .en(in_2[7]));
  assign controlled_buffer_4_out = decoder_1_out0 ? {5{1'b0}} : 5'bz;  // Controlled_Buffer controlled_buffer_4
  assign controlled_buffer_4_out = decoder_1_out1 ? 5'b00010 : 5'bz;  // Controlled_Buffer controlled_buffer_5
  assign controlled_buffer_4_out = decoder_1_out2 ? 5'b00100 : 5'bz;  // Controlled_Buffer controlled_buffer_6
  assign controlled_buffer_4_out = decoder_1_out3 ? 5'b00110 : 5'bz;  // Controlled_Buffer controlled_buffer_7
  Adder #(.width(5)) adder_2 (
    .a(5'b11000), .b(controlled_buffer_4_out), .out(controlled_buffer_1_out));  // open: cin, cout
  assign Params_OUT = in_2[3] ? out_4 : 16'bz;  // Controlled_Buffer controlled_buffer_8
  assign controlled_buffer_1_out = in_2[2] ? out_4[7:3] : 5'bz;  // Controlled_Buffer controlled_buffer_9
  assign bit_extender_2_out = {{4{out_4[11]}}, out_4[11:0]};  // Bit_Extender bit_extender_2
  assign Params_OUT = in_2[11] ? bit_extender_2_out : 16'bz;  // Controlled_Buffer controlled_buffer_10
  assign Params_OUT = or_1_out ? bit_extender_3_out : 16'bz;  // Controlled_Buffer controlled_buffer_11
  assign bit_extender_3_out = {{6{1'b0}}, {controlled_buffer_3_out, controlled_buffer_1_out}};  // Bit_Extender bit_extender_3
  or or_1 (or_1_out, in_2[10], in_2[9], in_2[8], in_2[7], in_2[2]);
  assign Bits_OUT = in_2[5] ? out_4[2:0] : 3'bz;  // Controlled_Buffer controlled_buffer_12
  assign Bits_OUT = in_2[6] ? out_4[6:4] : 3'bz;  // Controlled_Buffer controlled_buffer_13
  assign bit_extender_4_out = {{9{out_4[9]}}, out_4[9:3]};  // Bit_Extender bit_extender_4
  assign Params_OUT = in_2[4] ? bit_extender_4_out : 16'bz;  // Controlled_Buffer controlled_buffer_14
  assign Immediate_OUT = in_2[1] ? {out_4[11:8], out_4[3:0]} : 8'bz;  // Controlled_Buffer controlled_buffer_15
  assign Immediate_OUT = in_2[0] ? bit_extender_5_out : 8'bz;  // Controlled_Buffer controlled_buffer_16
  assign bit_extender_5_out = {{2{1'b0}}, {out_4[7:6], out_4[3:0]}};  // Bit_Extender bit_extender_5
  Pull_Resistor pull_resistor_1 (.node(Params_OUT));
  Pull_Resistor pull_resistor_2 (.node(Bits_OUT));
  Pull_Resistor pull_resistor_3 (.node(Immediate_OUT));

  // Notes on the sheet:
  //   RJMP Dest
  //   Rd 16-31
  //   Rr 0-31
  //   Rd 0-31
  //   Rd 24,26,28,30
  //   Bits hnb
  //   Bits lnb
  //   Branch
  //   INSTR
  //   IO 0-31
  //   8-Bit Im
  //   6-Bit Im
endmodule

// DEC
module Decoder (
  input  [15:0] in_1,
  output [31:0] CON2,
  output [31:0] CON1
);

  wire clock_1_out, clock_2_out, comparator_1_eq, comparator_2_eq, comparator_3_eq, comparator_4_eq,
       comparator_5_eq, comparator_6_eq, comparator_7_eq, comparator_8_eq, comparator_9_eq, comparator_10_eq,
       comparator_11_eq, comparator_12_eq, comparator_13_eq, comparator_14_eq, not_1_out;
  wire [7:0] adder_1_out, controlled_buffer_1_out, counter_1_q;
  wire [15:0] and_1_out, and_2_out, and_3_out, and_4_out, and_5_out, and_6_out, and_7_out, and_8_out,
       and_9_out, and_10_out, and_11_out, and_12_out, and_13_out, and_14_out, register_1_q;

  Register #(.width(16), .trigger("high")) register_1 (
    .D(in_1), .en(CON1[31]), .Q(register_1_q), .clk(clock_1_out));  // open: clr
  Clock clock_1 (.out(clock_1_out));
  assign and_1_out = 16'hfc00 & register_1_q;  // AND_Gate and_1, 16 bits wide
  assign and_2_out = 16'hfc00 & register_1_q;  // AND_Gate and_2, 16 bits wide
  assign and_3_out = 16'hf000 & register_1_q;  // AND_Gate and_3, 16 bits wide
  assign and_4_out = 16'hff00 & register_1_q;  // AND_Gate and_4, 16 bits wide
  assign and_5_out = 16'hf000 & register_1_q;  // AND_Gate and_5, 16 bits wide
  assign and_6_out = 16'hfc00 & register_1_q;  // AND_Gate and_6, 16 bits wide
  assign and_7_out = 16'hf000 & register_1_q;  // AND_Gate and_7, 16 bits wide
  assign and_8_out = 16'hfe0f & register_1_q;  // AND_Gate and_8, 16 bits wide
  assign and_9_out = 16'hff8f & register_1_q;  // AND_Gate and_9, 16 bits wide
  assign and_10_out = 16'hfe08 & register_1_q;  // AND_Gate and_10, 16 bits wide
  assign and_11_out = 16'hfc00 & register_1_q;  // AND_Gate and_11, 16 bits wide
  assign and_12_out = 16'hfc00 & register_1_q;  // AND_Gate and_12, 16 bits wide
  assign and_13_out = 16'hff8f & register_1_q;  // AND_Gate and_13, 16 bits wide
  assign and_14_out = 16'hfe08 & register_1_q;  // AND_Gate and_14, 16 bits wide
  not not_1 (not_1_out, CON1[31]);
  Clock clock_2 (.out(clock_2_out));
  assign controlled_buffer_1_out = comparator_1_eq ? 8'h1 : 8'bz;  // Controlled_Buffer controlled_buffer_1
  Comparator #(.width(16)) comparator_1 (.a(and_1_out), .b(16'h1c00), .eq(comparator_1_eq));  // open: gt, lt
  assign controlled_buffer_1_out = comparator_2_eq ? 8'h2 : 8'bz;  // Controlled_Buffer controlled_buffer_2
  Comparator #(.width(16)) comparator_2 (.a(and_2_out), .b(16'hc00), .eq(comparator_2_eq));  // open: gt, lt
  assign controlled_buffer_1_out = comparator_3_eq ? 8'h3 : 8'bz;  // Controlled_Buffer controlled_buffer_3
  Comparator #(.width(16)) comparator_3 (.a(and_3_out), .b(16'he000), .eq(comparator_3_eq));  // open: gt, lt
  assign controlled_buffer_1_out = comparator_4_eq ? 8'h4 : 8'bz;  // Controlled_Buffer controlled_buffer_4
  Comparator #(.width(16)) comparator_4 (.a(and_4_out), .b(16'h9600), .eq(comparator_4_eq));  // open: gt, lt
  assign controlled_buffer_1_out = comparator_5_eq ? 8'h6 : 8'bz;  // Controlled_Buffer controlled_buffer_5
  Comparator #(.width(16)) comparator_5 (.a(and_5_out), .b(16'hc000), .eq(comparator_5_eq));  // open: gt, lt
  assign controlled_buffer_1_out = comparator_6_eq ? 8'h7 : 8'bz;  // Controlled_Buffer controlled_buffer_6
  Comparator #(.width(16)) comparator_6 (.a(and_6_out), .b(16'h2000), .eq(comparator_6_eq));  // open: gt, lt
  assign controlled_buffer_1_out = comparator_7_eq ? 8'h8 : 8'bz;  // Controlled_Buffer controlled_buffer_7
  Comparator #(.width(16)) comparator_7 (.a(and_7_out), .b(16'h7000), .eq(comparator_7_eq));  // open: gt, lt
  assign controlled_buffer_1_out = comparator_8_eq ? 8'h9 : 8'bz;  // Controlled_Buffer controlled_buffer_8
  Comparator #(.width(16)) comparator_8 (.a(and_8_out), .b(16'h9405), .eq(comparator_8_eq));  // open: gt, lt
  assign controlled_buffer_1_out = comparator_9_eq ? 8'ha : 8'bz;  // Controlled_Buffer controlled_buffer_9
  Comparator #(.width(16)) comparator_9 (.a(and_9_out), .b(16'h9488), .eq(comparator_9_eq));  // open: gt, lt
  assign controlled_buffer_1_out = comparator_10_eq ? 8'hb : 8'bz;  // Controlled_Buffer controlled_buffer_10
  Comparator #(.width(16)) comparator_10 (.a(and_10_out), .b(16'hf800), .eq(comparator_10_eq));  // open: gt, lt
  assign controlled_buffer_1_out = comparator_11_eq ? 8'hc : 8'bz;  // Controlled_Buffer controlled_buffer_11
  Comparator #(.width(16)) comparator_11 (.a(and_11_out), .b(16'hf400), .eq(comparator_11_eq));  // open: gt, lt
  assign controlled_buffer_1_out = comparator_12_eq ? 8'hd : 8'bz;  // Controlled_Buffer controlled_buffer_12
  Comparator #(.width(16)) comparator_12 (.a(and_12_out), .b(16'hf000), .eq(comparator_12_eq));  // open: gt, lt
  assign controlled_buffer_1_out = comparator_13_eq ? 8'he : 8'bz;  // Controlled_Buffer controlled_buffer_13
  Comparator #(.width(16)) comparator_13 (.a(and_13_out), .b(16'h9408), .eq(comparator_13_eq));  // open: gt, lt
  assign controlled_buffer_1_out = comparator_14_eq ? 8'hf : 8'bz;  // Controlled_Buffer controlled_buffer_14
  Comparator #(.width(16)) comparator_14 (.a(and_14_out), .b(16'hfa00), .eq(comparator_14_eq));  // open: gt, lt
  Counter counter_1 (
    .load(CON1[31]), .D({8{1'b0}}), .count(not_1_out), .Q(counter_1_q), .clk(clock_2_out));  // open: carry, clr
  Pull_Resistor pull_resistor_1 (.node(controlled_buffer_1_out));
  // Probe on adder_1_out
  Adder adder_1 (.a(counter_1_q), .b(controlled_buffer_1_out), .out(adder_1_out));  // open: cin, cout
  ROM #(.dataWidth(32)) rom_1 (.addr(adder_1_out), .data(CON1));  // open: sel
  ROM #(.dataWidth(32)) rom_2 (.addr(adder_1_out), .data(CON2));  // open: sel

  // Notes on the sheet:
  //   ADC
  //   ADD
  //   LDI
  //   ADIW
  //   RJMP
  //   AND
  //   ANDI
  //   ASR
  //   BCLR
  //   BLD
  //   BRBC
  //   BRBS
  //   BSET
  //   BST
  //   contents of rom_1 (hex, n*v repeats v):
  //   88000000 8809c300 8805c300 88404402 44c081 880ac080 c0000800 880dc300 884cc202 8820c200 88000040
  //   8800c220 88000030 88000030 88000040 88008220
  //   contents of rom_2 (hex, n*v repeats v):
  //   10*0 11fe00 17e38 17e80 17f00 21fe00 c0fe00
endmodule

module SREG (
  input  [2:0] Bits,
  input  Clr,
  input  Set,
  input  Write,
  input  Read,
  input  [7:0] Data_Bus_IN,
  input  [7:0] From_ALU,
  input  ALU_Write,
  output [7:0] Data_Bus_OUT,
  output [7:0] To_ALU
);

  wire clock_1_out, or_2_out;
  wire [7:0] bitmanipulator_1_modified, or_1_out, pull_resistor_1_node;

  Pull_Resistor pull_resistor_1 (.node(pull_resistor_1_node));
  BitManipulator bitmanipulator_1 (
    .Modified(bitmanipulator_1_modified), .Bit(Bits), .CLR(Clr), .SET(Set), .Initial(To_ALU));
  assign or_1_out = pull_resistor_1_node | bitmanipulator_1_modified | From_ALU;  // OR_Gate or_1, 8 bits wide
  Register register_1 (.D(or_1_out), .en(or_2_out), .Q(To_ALU), .clk(clock_1_out));  // open: clr
  or or_2 (or_2_out, Write, ALU_Write);
  Clock clock_1 (.out(clock_1_out));
  assign pull_resistor_1_node = Write ? Data_Bus_IN : 8'bz;  // Controlled_Buffer controlled_buffer_1
  assign Data_Bus_OUT = Read ? To_ALU : 8'bz;  // Controlled_Buffer controlled_buffer_2
endmodule

// Registers
module RegisterFileV2 (
  input  [2:0] Bit_to_set,
  input  [2:0] Bit_to_read,
  input  [9:0] Rd_Addr,
  input  [31:0] CONTROL,
  input  Bit_Load,
  input  [7:0] DATA_IN,
  output [15:0] Reg_Pair_OUT,
  output [7:0] Rd_OUT,
  output [7:0] Rr_OUT
);

  wire clock_1_out, comparator_1_eq, decoder_1_out0, decoder_1_out1, decoder_1_out2, decoder_1_out3,
       decoder_1_out4, decoder_1_out5, decoder_1_out6, decoder_1_out7, decoder_1_out8, decoder_1_out9,
       decoder_1_out10, decoder_1_out11, decoder_1_out12, decoder_1_out13, decoder_1_out14, decoder_1_out15,
       decoder_1_out16, decoder_1_out17, decoder_1_out18, decoder_1_out19, decoder_1_out20, decoder_1_out21,
       decoder_1_out22, decoder_1_out23, decoder_1_out24, decoder_1_out25, decoder_1_out26, decoder_1_out27,
       decoder_1_out28, decoder_1_out29, decoder_1_out30, decoder_1_out31, decoder_2_out0, decoder_2_out1,
       decoder_2_out2, decoder_2_out3, decoder_2_out4, decoder_2_out5, decoder_2_out6, decoder_2_out7,
       decoder_2_out8, decoder_2_out9, decoder_2_out10, decoder_2_out11, decoder_2_out12, decoder_2_out13,
       decoder_2_out14, decoder_2_out15, decoder_2_out16, decoder_2_out17, decoder_2_out18, decoder_2_out19,
       decoder_2_out20, decoder_2_out21, decoder_2_out22, decoder_2_out23, decoder_2_out24, decoder_2_out25,
       decoder_2_out26, decoder_2_out27, decoder_2_out28, decoder_2_out29, decoder_2_out30, decoder_2_out31,
       decoder_3_out0, decoder_3_out1, decoder_3_out2, decoder_3_out3, decoder_3_out4, decoder_3_out5,
       decoder_3_out6, decoder_3_out7, decoder_3_out8, decoder_3_out9, decoder_3_out10, decoder_3_out11,
       decoder_3_out12, decoder_3_out13, decoder_3_out14, decoder_3_out15, decoder_3_out16, decoder_3_out17,
       decoder_3_out18, decoder_3_out19, decoder_3_out20, decoder_3_out21, decoder_3_out22, decoder_3_out23,
       decoder_3_out24, decoder_3_out25, decoder_3_out26, decoder_3_out27, decoder_3_out28, decoder_3_out29,
       decoder_3_out30, decoder_3_out31, not_1_out, not_2_out, not_3_out, not_4_out, not_5_out, or_1_out,
       or_2_out, or_3_out, pull_resistor_5_node;
  wire [4:0] adder_1_out, adder_2_out, controlled_buffer_2_out, controlled_buffer_4_out;
  wire [7:0] and_1_out, bitmanipulator_1_modified, controlled_buffer_6_out, controlled_buffer_7_out,
       controlled_buffer_8_out, controlled_buffer_9_out, controlled_buffer_10_out, controlled_buffer_11_out,
       controlled_buffer_12_out, controlled_buffer_13_out, controlled_buffer_16_out,
       controlled_buffer_21_out, controlled_buffer_26_out, controlled_buffer_31_out,
       controlled_buffer_36_out, controlled_buffer_41_out, controlled_buffer_46_out,
       controlled_buffer_51_out, controlled_buffer_56_out, controlled_buffer_59_out,
       controlled_buffer_62_out, controlled_buffer_65_out, controlled_buffer_68_out,
       controlled_buffer_71_out, controlled_buffer_74_out, controlled_buffer_77_out,
       controlled_buffer_81_out, controlled_buffer_84_out, controlled_buffer_87_out,
       controlled_buffer_90_out, controlled_buffer_93_out, controlled_buffer_96_out,
       controlled_buffer_99_out, controlled_buffer_102_out, or_4_out, pull_resistor_2_node,
       pull_resistor_3_node, register_1_q, register_2_q, register_3_q, register_4_q, register_5_q,
       register_6_q, register_7_q, register_8_q, register_9_q, register_10_q, register_11_q, register_12_q,
       register_13_q, register_14_q, register_15_q, register_16_q, register_17_q, register_18_q,
       register_19_q, register_20_q, register_21_q, register_22_q, register_23_q, register_24_q,
       register_25_q, register_26_q, register_27_q, register_28_q, register_29_q, register_30_q,
       register_31_q, register_32_q, shifter_1_out;

  Decoder_part #(.select(5), .disabled(0)) decoder_1 (
    .out0(decoder_1_out0), .out1(decoder_1_out1), .out2(decoder_1_out2), .out3(decoder_1_out3),
    .out4(decoder_1_out4), .out5(decoder_1_out5), .out6(decoder_1_out6), .out7(decoder_1_out7),
    .out8(decoder_1_out8), .out9(decoder_1_out9), .out10(decoder_1_out10), .out11(decoder_1_out11),
    .out12(decoder_1_out12), .out13(decoder_1_out13), .out14(decoder_1_out14), .out15(decoder_1_out15),
    .out16(decoder_1_out16), .out17(decoder_1_out17), .out18(decoder_1_out18), .out19(decoder_1_out19),
    .out20(decoder_1_out20), .out21(decoder_1_out21), .out22(decoder_1_out22), .out23(decoder_1_out23),
    .out24(decoder_1_out24), .out25(decoder_1_out25), .out26(decoder_1_out26), .out27(decoder_1_out27),
    .out28(decoder_1_out28), .out29(decoder_1_out29), .out30(decoder_1_out30), .out31(decoder_1_out31),
    .sel(controlled_buffer_4_out), .en(or_3_out));
  Decoder_part #(.select(5), .disabled(0)) decoder_2 (
    .out0(decoder_2_out0), .out1(decoder_2_out1), .out2(decoder_2_out2), .out3(decoder_2_out3),
    .out4(decoder_2_out4), .out5(decoder_2_out5), .out6(decoder_2_out6), .out7(decoder_2_out7),
    .out8(decoder_2_out8), .out9(decoder_2_out9), .out10(decoder_2_out10), .out11(decoder_2_out11),
    .out12(decoder_2_out12), .out13(decoder_2_out13), .out14(decoder_2_out14), .out15(decoder_2_out15),
    .out16(decoder_2_out16), .out17(decoder_2_out17), .out18(decoder_2_out18), .out19(decoder_2_out19),
    .out20(decoder_2_out20), .out21(decoder_2_out21), .out22(decoder_2_out22), .out23(decoder_2_out23),
    .out24(decoder_2_out24), .out25(decoder_2_out25), .out26(decoder_2_out26), .out27(decoder_2_out27),
    .out28(decoder_2_out28), .out29(decoder_2_out29), .out30(decoder_2_out30), .out31(decoder_2_out31),
    .sel(controlled_buffer_2_out), .en(or_1_out));
  Decoder_part #(.select(5), .disabled(0)) decoder_3 (
    .out0(decoder_3_out0), .out1(decoder_3_out1), .out2(decoder_3_out2), .out3(decoder_3_out3),
    .out4(decoder_3_out4), .out5(decoder_3_out5), .out6(decoder_3_out6), .out7(decoder_3_out7),
    .out8(decoder_3_out8), .out9(decoder_3_out9), .out10(decoder_3_out10), .out11(decoder_3_out11),
    .out12(decoder_3_out12), .out13(decoder_3_out13), .out14(decoder_3_out14), .out15(decoder_3_out15),
    .out16(decoder_3_out16), .out17(decoder_3_out17), .out18(decoder_3_out18), .out19(decoder_3_out19),
    .out20(decoder_3_out20), .out21(decoder_3_out21), .out22(decoder_3_out22), .out23(decoder_3_out23),
    .out24(decoder_3_out24), .out25(decoder_3_out25), .out26(decoder_3_out26), .out27(decoder_3_out27),
    .out28(decoder_3_out28), .out29(decoder_3_out29), .out30(decoder_3_out30), .out31(decoder_3_out31),
    .sel(controlled_buffer_2_out), .en(or_2_out));
  or or_1 (or_1_out, CONTROL[13], CONTROL[14]);
  Pull_Resistor pull_resistor_1 (.node(Reg_Pair_OUT));
  assign Reg_Pair_OUT = CONTROL[12] ? {Rr_OUT, Rd_OUT} : 16'bz;  // Controlled_Buffer controlled_buffer_1
  or or_2 (or_2_out, CONTROL[12], CONTROL[15]);
  or or_3 (or_3_out, CONTROL[13], CONTROL[12], CONTROL[16]);
  not not_1 (not_1_out, CONTROL[17]);
  assign controlled_buffer_2_out = not_1_out ? Rd_Addr[4:0] : 5'bz;  // Controlled_Buffer controlled_buffer_2
  assign controlled_buffer_2_out = CONTROL[17] ? adder_2_out : 5'bz;  // Controlled_Buffer controlled_buffer_3
  not not_2 (not_2_out, CONTROL[12]);
  assign controlled_buffer_4_out = not_2_out ? Rd_Addr[9:5] : 5'bz;  // Controlled_Buffer controlled_buffer_4
  assign controlled_buffer_4_out = CONTROL[12] ? adder_1_out : 5'bz;  // Controlled_Buffer controlled_buffer_5
  Adder #(.width(5)) adder_1 (.a(Rd_Addr[4:0]), .b(5'b00001), .out(adder_1_out));  // open: cin, cout
  Adder #(.width(5)) adder_2 (.a(Rd_Addr[4:0]), .b(5'b00001), .out(adder_2_out));  // open: cin, cout
  Clock clock_1 (.out(clock_1_out));
  Register register_1 (
    .D(controlled_buffer_6_out), .en(decoder_2_out0), .Q(register_1_q), .clk(clock_1_out));  // open: clr
  assign controlled_buffer_6_out = decoder_2_out0 ? or_4_out : 8'bz;  // Controlled_Buffer controlled_buffer_6
  Register register_2 (
    .D(controlled_buffer_7_out), .en(decoder_2_out4), .Q(register_2_q), .clk(clock_1_out));  // open: clr
  assign controlled_buffer_7_out = decoder_2_out4 ? or_4_out : 8'bz;  // Controlled_Buffer controlled_buffer_7
  assign controlled_buffer_8_out = decoder_2_out8 ? or_4_out : 8'bz;  // Controlled_Buffer controlled_buffer_8
  Register register_3 (
    .D(controlled_buffer_8_out), .en(decoder_2_out8), .Q(register_3_q), .clk(clock_1_out));  // open: clr
  assign controlled_buffer_9_out = decoder_2_out12 ? or_4_out : 8'bz;  // Controlled_Buffer controlled_buffer_9
  Register register_4 (
    .D(controlled_buffer_9_out), .en(decoder_2_out12), .Q(register_4_q), .clk(clock_1_out));  // open: clr
  assign controlled_buffer_10_out = decoder_2_out16 ? or_4_out : 8'bz;  // Controlled_Buffer controlled_buffer_10
  Register register_5 (
    .D(controlled_buffer_10_out), .en(decoder_2_out16), .Q(register_5_q), .clk(clock_1_out));  // open: clr
  assign controlled_buffer_11_out = decoder_2_out20 ? or_4_out : 8'bz;  // Controlled_Buffer controlled_buffer_11
  Register register_6 (
    .D(controlled_buffer_11_out), .en(decoder_2_out20), .Q(register_6_q), .clk(clock_1_out));  // open: clr
  assign controlled_buffer_12_out = decoder_2_out24 ? or_4_out : 8'bz;  // Controlled_Buffer controlled_buffer_12
  Register register_7 (
    .D(controlled_buffer_12_out), .en(decoder_2_out24), .Q(register_7_q), .clk(clock_1_out));  // open: clr
  assign controlled_buffer_13_out = decoder_2_out28 ? or_4_out : 8'bz;  // Controlled_Buffer controlled_buffer_13
  Register register_8 (
    .D(controlled_buffer_13_out), .en(decoder_2_out28), .Q(register_8_q), .clk(clock_1_out));  // open: clr
  // Probe on pull_resistor_2_node
  assign Rr_OUT = decoder_1_out0 ? register_1_q : 8'bz;  // Controlled_Buffer controlled_buffer_14
  assign Rr_OUT = decoder_1_out1 ? register_9_q : 8'bz;  // Controlled_Buffer controlled_buffer_15
  Register register_9 (
    .D(controlled_buffer_16_out), .en(decoder_2_out1), .Q(register_9_q), .clk(clock_1_out));  // open: clr
  assign controlled_buffer_16_out = decoder_2_out1 ? or_4_out : 8'bz;  // Controlled_Buffer controlled_buffer_16
  assign Rd_OUT = decoder_3_out1 ? register_9_q : 8'bz;  // Controlled_Buffer controlled_buffer_17
  assign Rd_OUT = decoder_3_out0 ? register_1_q : 8'bz;  // Controlled_Buffer controlled_buffer_18
  assign Rr_OUT = decoder_1_out4 ? register_2_q : 8'bz;  // Controlled_Buffer controlled_buffer_19
  assign Rr_OUT = decoder_1_out5 ? register_10_q : 8'bz;  // Controlled_Buffer controlled_buffer_20
  Register register_10 (
    .D(controlled_buffer_21_out), .en(decoder_2_out5), .Q(register_10_q), .clk(clock_1_out));  // open: clr
  assign controlled_buffer_21_out = decoder_2_out5 ? or_4_out : 8'bz;  // Controlled_Buffer controlled_buffer_21
  assign Rd_OUT = decoder_3_out5 ? register_10_q : 8'bz;  // Controlled_Buffer controlled_buffer_22
  assign Rd_OUT = decoder_3_out4 ? register_2_q : 8'bz;  // Controlled_Buffer controlled_buffer_23
  assign Rr_OUT = decoder_1_out9 ? register_11_q : 8'bz;  // Controlled_Buffer controlled_buffer_24
  assign Rr_OUT = decoder_1_out8 ? register_3_q : 8'bz;  // Controlled_Buffer controlled_buffer_25
  Register register_11 (
    .D(controlled_buffer_26_out), .en(decoder_2_out9), .Q(register_11_q), .clk(clock_1_out));  // open: clr
  assign controlled_buffer_26_out = decoder_2_out9 ? or_4_out : 8'bz;  // Controlled_Buffer controlled_buffer_26
  assign Rd_OUT = decoder_3_out8 ? register_3_q : 8'bz;  // Controlled_Buffer controlled_buffer_27
  assign Rd_OUT = decoder_3_out9 ? register_11_q : 8'bz;  // Controlled_Buffer controlled_buffer_28
  assign Rr_OUT = decoder_1_out13 ? register_12_q : 8'bz;  // Controlled_Buffer controlled_buffer_29
  assign Rr_OUT = decoder_1_out12 ? register_4_q : 8'bz;  // Controlled_Buffer controlled_buffer_30
  assign controlled_buffer_31_out = decoder_2_out13 ? or_4_out : 8'bz;  // Controlled_Buffer controlled_buffer_31
  Register register_12 (
    .D(controlled_buffer_31_out), .en(decoder_2_out13), .Q(register_12_q), .clk(clock_1_out));  // open: clr
  assign Rd_OUT = decoder_3_out12 ? register_4_q : 8'bz;  // Controlled_Buffer controlled_buffer_32
  assign Rd_OUT = decoder_3_out13 ? register_12_q : 8'bz;  // Controlled_Buffer controlled_buffer_33
  assign Rr_OUT = decoder_1_out16 ? register_5_q : 8'bz;  // Controlled_Buffer controlled_buffer_34
  assign Rr_OUT = decoder_1_out17 ? register_13_q : 8'bz;  // Controlled_Buffer controlled_buffer_35
  Register register_13 (
    .D(controlled_buffer_36_out), .en(decoder_2_out17), .Q(register_13_q), .clk(clock_1_out));  // open: clr
  assign controlled_buffer_36_out = decoder_2_out17 ? or_4_out : 8'bz;  // Controlled_Buffer controlled_buffer_36
  assign Rd_OUT = decoder_3_out16 ? register_5_q : 8'bz;  // Controlled_Buffer controlled_buffer_37
  assign Rd_OUT = decoder_3_out17 ? register_13_q : 8'bz;  // Controlled_Buffer controlled_buffer_38
  assign Rr_OUT = decoder_1_out20 ? register_6_q : 8'bz;  // Controlled_Buffer controlled_buffer_39
  assign Rr_OUT = decoder_1_out21 ? register_14_q : 8'bz;  // Controlled_Buffer controlled_buffer_40
  Register register_14 (
    .D(controlled_buffer_41_out), .en(decoder_2_out21), .Q(register_14_q), .clk(clock_1_out));  // open: clr
  assign controlled_buffer_41_out = decoder_2_out21 ? or_4_out : 8'bz;  // Controlled_Buffer controlled_buffer_41
  assign Rd_OUT = decoder_3_out20 ? register_6_q : 8'bz;  // Controlled_Buffer controlled_buffer_42
  assign Rd_OUT = decoder_3_out21 ? register_14_q : 8'bz;  // Controlled_Buffer controlled_buffer_43
  assign Rr_OUT = decoder_1_out25 ? register_15_q : 8'bz;  // Controlled_Buffer controlled_buffer_44
  assign Rr_OUT = decoder_1_out24 ? register_7_q : 8'bz;  // Controlled_Buffer controlled_buffer_45
  Register register_15 (
    .D(controlled_buffer_46_out), .en(decoder_2_out25), .Q(register_15_q), .clk(clock_1_out));  // open: clr
  assign controlled_buffer_46_out = decoder_2_out25 ? or_4_out : 8'bz;  // Controlled_Buffer controlled_buffer_46
  assign Rd_OUT = decoder_3_out24 ? register_7_q : 8'bz;  // Controlled_Buffer controlled_buffer_47
  assign Rd_OUT = decoder_3_out25 ? register_15_q : 8'bz;  // Controlled_Buffer controlled_buffer_48
  assign Rr_OUT = decoder_1_out28 ? register_8_q : 8'bz;  // Controlled_Buffer controlled_buffer_49
  assign Rr_OUT = decoder_1_out29 ? register_16_q : 8'bz;  // Controlled_Buffer controlled_buffer_50
  assign controlled_buffer_51_out = decoder_2_out29 ? or_4_out : 8'bz;  // Controlled_Buffer controlled_buffer_51
  Register register_16 (
    .D(controlled_buffer_51_out), .en(decoder_2_out29), .Q(register_16_q), .clk(clock_1_out));  // open: clr
  assign Rd_OUT = decoder_3_out29 ? register_16_q : 8'bz;  // Controlled_Buffer controlled_buffer_52
  assign Rd_OUT = decoder_3_out28 ? register_8_q : 8'bz;  // Controlled_Buffer controlled_buffer_53
  Pull_Resistor pull_resistor_2 (.node(pull_resistor_2_node));
  assign pull_resistor_2_node = Bit_Load ? bitmanipulator_1_modified : 8'bz;  // Controlled_Buffer controlled_buffer_54
  assign Rr_OUT = decoder_1_out2 ? register_17_q : 8'bz;  // Controlled_Buffer controlled_buffer_55
  Register register_17 (
    .D(controlled_buffer_56_out), .en(decoder_2_out2), .Q(register_17_q), .clk(clock_1_out));  // open: clr
  assign controlled_buffer_56_out = decoder_2_out2 ? or_4_out : 8'bz;  // Controlled_Buffer controlled_buffer_56
  assign Rd_OUT = decoder_3_out2 ? register_17_q : 8'bz;  // Controlled_Buffer controlled_buffer_57
  assign Rr_OUT = decoder_1_out6 ? register_18_q : 8'bz;  // Controlled_Buffer controlled_buffer_58
  Register register_18 (
    .D(controlled_buffer_59_out), .en(decoder_2_out6), .Q(register_18_q), .clk(clock_1_out));  // open: clr
  assign controlled_buffer_59_out = decoder_2_out6 ? or_4_out : 8'bz;  // Controlled_Buffer controlled_buffer_59
  assign Rd_OUT = decoder_3_out6 ? register_18_q : 8'bz;  // Controlled_Buffer controlled_buffer_60
  assign Rr_OUT = decoder_1_out10 ? register_19_q : 8'bz;  // Controlled_Buffer controlled_buffer_61
  Register register_19 (
    .D(controlled_buffer_62_out), .en(decoder_2_out10), .Q(register_19_q), .clk(clock_1_out));  // open: clr
  assign controlled_buffer_62_out = decoder_2_out10 ? or_4_out : 8'bz;  // Controlled_Buffer controlled_buffer_62
  assign Rd_OUT = decoder_3_out10 ? register_19_q : 8'bz;  // Controlled_Buffer controlled_buffer_63
  assign Rr_OUT = decoder_1_out14 ? register_20_q : 8'bz;  // Controlled_Buffer controlled_buffer_64
  Register register_20 (
    .D(controlled_buffer_65_out), .en(decoder_2_out14), .Q(register_20_q), .clk(clock_1_out));  // open: clr
  assign controlled_buffer_65_out = decoder_2_out14 ? or_4_out : 8'bz;  // Controlled_Buffer controlled_buffer_65
  assign Rd_OUT = decoder_3_out14 ? register_20_q : 8'bz;  // Controlled_Buffer controlled_buffer_66
  assign Rr_OUT = decoder_1_out18 ? register_21_q : 8'bz;  // Controlled_Buffer controlled_buffer_67
  assign controlled_buffer_68_out = decoder_2_out18 ? or_4_out : 8'bz;  // Controlled_Buffer controlled_buffer_68
  Register register_21 (
    .D(controlled_buffer_68_out), .en(decoder_2_out18), .Q(register_21_q), .clk(clock_1_out));  // open: clr
  assign Rd_OUT = decoder_3_out18 ? register_21_q : 8'bz;  // Controlled_Buffer controlled_buffer_69
  assign Rr_OUT = decoder_1_out22 ? register_22_q : 8'bz;  // Controlled_Buffer controlled_buffer_70
  assign controlled_buffer_71_out = decoder_2_out22 ? or_4_out : 8'bz;  // Controlled_Buffer controlled_buffer_71
  Register register_22 (
    .D(controlled_buffer_71_out), .en(decoder_2_out22), .Q(register_22_q), .clk(clock_1_out));  // open: clr
  assign Rd_OUT = decoder_3_out22 ? register_22_q : 8'bz;  // Controlled_Buffer controlled_buffer_72
  assign Rr_OUT = decoder_1_out26 ? register_23_q : 8'bz;  // Controlled_Buffer controlled_buffer_73
  assign controlled_buffer_74_out = decoder_2_out26 ? or_4_out : 8'bz;  // Controlled_Buffer controlled_buffer_74
  Register register_23 (
    .D(controlled_buffer_74_out), .en(decoder_2_out26), .Q(register_23_q), .clk(clock_1_out));  // open: clr
  assign Rd_OUT = decoder_3_out26 ? register_23_q : 8'bz;  // Controlled_Buffer controlled_buffer_75
  assign Rr_OUT = decoder_1_out30 ? register_24_q : 8'bz;  // Controlled_Buffer controlled_buffer_76
  Register register_24 (
    .D(controlled_buffer_77_out), .en(decoder_2_out30), .Q(register_24_q), .clk(clock_1_out));  // open: clr
  assign controlled_buffer_77_out = decoder_2_out30 ? or_4_out : 8'bz;  // Controlled_Buffer controlled_buffer_77
  assign Rd_OUT = decoder_3_out30 ? register_24_q : 8'bz;  // Controlled_Buffer controlled_buffer_78
  assign and_1_out = shifter_1_out & DATA_IN;  // AND_Gate and_1, 8 bits wide
  Comparator comparator_1 (.a(and_1_out), .b({8{1'b0}}), .eq(comparator_1_eq));  // open: gt, lt
  not not_3 (not_3_out, comparator_1_eq);
  BitManipulator bitmanipulator_1 (
    .Modified(bitmanipulator_1_modified), .Bit(Bit_to_set), .CLR(comparator_1_eq), .SET(not_3_out),
    .Initial(Rd_OUT));
  assign or_4_out = pull_resistor_2_node | pull_resistor_3_node;  // OR_Gate or_4, 8 bits wide
  Pull_Resistor pull_resistor_3 (.node(pull_resistor_3_node));
  assign pull_resistor_3_node = CONTROL[13] ? Rr_OUT : 8'bz;  // Controlled_Buffer controlled_buffer_79
  assign Rr_OUT = decoder_1_out3 ? register_25_q : 8'bz;  // Controlled_Buffer controlled_buffer_80
  assign controlled_buffer_81_out = decoder_2_out3 ? or_4_out : 8'bz;  // Controlled_Buffer controlled_buffer_81
  Register register_25 (
    .D(controlled_buffer_81_out), .en(decoder_2_out3), .Q(register_25_q), .clk(clock_1_out));  // open: clr
  assign Rd_OUT = decoder_3_out3 ? register_25_q : 8'bz;  // Controlled_Buffer controlled_buffer_82
  assign Rr_OUT = decoder_1_out7 ? register_26_q : 8'bz;  // Controlled_Buffer controlled_buffer_83
  Register register_26 (
    .D(controlled_buffer_84_out), .en(decoder_2_out7), .Q(register_26_q), .clk(clock_1_out));  // open: clr
  assign controlled_buffer_84_out = decoder_2_out7 ? or_4_out : 8'bz;  // Controlled_Buffer controlled_buffer_84
  assign Rd_OUT = decoder_3_out7 ? register_26_q : 8'bz;  // Controlled_Buffer controlled_buffer_85
  assign Rr_OUT = decoder_1_out11 ? register_27_q : 8'bz;  // Controlled_Buffer controlled_buffer_86
  Register register_27 (
    .D(controlled_buffer_87_out), .en(decoder_2_out11), .Q(register_27_q), .clk(clock_1_out));  // open: clr
  assign controlled_buffer_87_out = decoder_2_out11 ? or_4_out : 8'bz;  // Controlled_Buffer controlled_buffer_87
  assign Rd_OUT = decoder_3_out11 ? register_27_q : 8'bz;  // Controlled_Buffer controlled_buffer_88
  assign Rr_OUT = decoder_1_out15 ? register_28_q : 8'bz;  // Controlled_Buffer controlled_buffer_89
  assign controlled_buffer_90_out = decoder_2_out15 ? or_4_out : 8'bz;  // Controlled_Buffer controlled_buffer_90
  Register register_28 (
    .D(controlled_buffer_90_out), .en(decoder_2_out15), .Q(register_28_q), .clk(clock_1_out));  // open: clr
  assign Rd_OUT = decoder_3_out15 ? register_28_q : 8'bz;  // Controlled_Buffer controlled_buffer_91
  assign Rr_OUT = decoder_1_out19 ? register_29_q : 8'bz;  // Controlled_Buffer controlled_buffer_92
  Register register_29 (
    .D(controlled_buffer_93_out), .en(decoder_2_out19), .Q(register_29_q), .clk(clock_1_out));  // open: clr
  assign controlled_buffer_93_out = decoder_2_out19 ? or_4_out : 8'bz;  // Controlled_Buffer controlled_buffer_93
  assign Rd_OUT = decoder_3_out19 ? register_29_q : 8'bz;  // Controlled_Buffer controlled_buffer_94
  assign Rr_OUT = decoder_1_out23 ? register_30_q : 8'bz;  // Controlled_Buffer controlled_buffer_95
  Register register_30 (
    .D(controlled_buffer_96_out), .en(decoder_2_out23), .Q(register_30_q), .clk(clock_1_out));  // open: clr
  assign controlled_buffer_96_out = decoder_2_out23 ? or_4_out : 8'bz;  // Controlled_Buffer controlled_buffer_96
  assign Rd_OUT = decoder_3_out23 ? register_30_q : 8'bz;  // Controlled_Buffer controlled_buffer_97
  assign Rr_OUT = decoder_1_out27 ? register_31_q : 8'bz;  // Controlled_Buffer controlled_buffer_98
  Register register_31 (
    .D(controlled_buffer_99_out), .en(decoder_2_out27), .Q(register_31_q), .clk(clock_1_out));  // open: clr
  assign controlled_buffer_99_out = decoder_2_out27 ? or_4_out : 8'bz;  // Controlled_Buffer controlled_buffer_99
  assign Rd_OUT = decoder_3_out27 ? register_31_q : 8'bz;  // Controlled_Buffer controlled_buffer_100
  assign Rr_OUT = decoder_1_out31 ? register_32_q : 8'bz;  // Controlled_Buffer controlled_buffer_101
  Register register_32 (
    .D(controlled_buffer_102_out), .en(decoder_2_out31), .Q(register_32_q), .clk(clock_1_out));  // open: clr
  assign controlled_buffer_102_out = decoder_2_out31 ? or_4_out : 8'bz;  // Controlled_Buffer controlled_buffer_102
  assign Rd_OUT = decoder_3_out31 ? register_32_q : 8'bz;  // Controlled_Buffer controlled_buffer_103
  Pull_Resistor pull_resistor_4 (.node(Rd_OUT));
  not not_4 (not_4_out, Bit_Load);
  not not_5 (not_5_out, CONTROL[13]);
  Pull_Resistor pull_resistor_5 (.node(pull_resistor_5_node));
  assign pull_resistor_5_node = not_4_out ? not_5_out : 1'bz;  // Controlled_Buffer controlled_buffer_104
  assign pull_resistor_3_node = pull_resistor_5_node ? DATA_IN : 8'bz;  // Controlled_Buffer controlled_buffer_105
  // Probe on or_4_out
  Pull_Resistor pull_resistor_6 (.node(Rr_OUT));
  Shifter shifter_1 (.in(8'h1), .\dist (Bit_to_read), .out(shifter_1_out));

  // Notes on the sheet:
  //   Read Pair
  //   MOVE
  //   Rd Write
  //   Rd Read
  //   Rr Read
  //   +1 Offset
endmodule

// IO
module IOMem (
  input  Write,
  input  Read,
  input  [2:0] BitToMod,
  input  BM_CLR,
  input  BM_SET,
  input  [7:0] DATA_IN,
  input  [5:0] Address,
  input  SP_Push,
  input  SP_Pop,
  input  SREG_LDT,
  input  [7:0] SREG_IN,
  input  SREG_ALU_EN,
  output [7:0] DATA_OUT,
  output [15:0] SP_OUT,
  output [7:0] SREG_OUT
);

  wire and_2_out, and_3_out, and_4_out, BM_EN, CLK, clock_2_out, comparator_1_eq, comparator_1_lt,
       controlled_buffer_3_out, controlled_buffer_4_out, controlled_buffer_5_out, not_1_out, not_3_out,
       not_4_out, or_1_out, or_4_out, or_5_out, or_6_out, or_8_out, or_9_out, pull_resistor_7_node, SPH_EN,
       SPL_EN, SREG_EN;
  wire [7:0] adder_1_out, adder_1_out_2, and_1_out, bitmanipulator_2_modified, BM_OUT,
       controlled_buffer_7_out, controlled_buffer_11_out, or_2_out, or_3_out, or_7_out, pull_resistor_6_node,
       register_1_q, register_2_q, shifter_1_out;
  wire [15:0] controlled_buffer_1_out, controlled_buffer_13_out, negator_1_out, pull_resistor_11_node;

  not not_1 (not_1_out, Address[5]);
  Decoder_part #(.select(5), .disabled(0)) decoder_1 (
    .sel(Address[4:0]), .en(not_1_out));  // open: out0, out1, out2, out3, out4, out5, out6, out7, out8, out9, out10, out11, out12, out13, out14, out15, out16, out17, out18, out19, out20, out21, out22, out23, out24, out25, out26, out27, out28, out29, out30, out31
  Decoder_part #(.select(5), .disabled(0)) decoder_2 (
    .out29(SPL_EN), .out30(SPH_EN), .out31(SREG_EN), .sel(Address[4:0]), .en(Address[5]));  // open: out0, out1, out2, out3, out4, out5, out6, out7, out8, out9, out10, out11, out12, out13, out14, out15, out16, out17, out18, out19, out20, out21, out22, out23, out24, out25, out26, out27, out28
  Clock clock_1 (.out(CLK));
  Pull_Resistor pull_resistor_1 (.node(DATA_OUT));
  BitManipulator bitmanipulator_1 (.Modified(BM_OUT), .Bit(BitToMod), .CLR(BM_CLR), .SET(BM_SET), .Initial(DATA_OUT));
  not not_2 (BM_EN, or_1_out);
  or or_1 (or_1_out, BM_CLR, BM_SET);
  assign or_2_out = adder_1_out_2 | DATA_IN;  // OR_Gate or_2, 8 bits wide
  assign or_3_out = adder_1_out | DATA_IN;  // OR_Gate or_3, 8 bits wide
  assign controlled_buffer_1_out = SP_Pop ? 16'h1 : 16'bz;  // Controlled_Buffer controlled_buffer_1
  Pull_Resistor pull_resistor_2 (.node(controlled_buffer_1_out));
  assign controlled_buffer_1_out = SP_Push ? negator_1_out : 16'bz;  // Controlled_Buffer controlled_buffer_2
  Negator #(.width(16)) negator_1 (.in(16'h1), .out(negator_1_out));
  Register register_1 (.D(or_2_out), .en(or_4_out), .Q(register_1_q), .clk(clock_2_out));  // open: clr
  or or_4 (or_4_out, or_8_out, controlled_buffer_3_out);
  assign controlled_buffer_3_out = Write ? SPH_EN : 1'bz;  // Controlled_Buffer controlled_buffer_3
  Pull_Resistor pull_resistor_3 (.node(controlled_buffer_3_out));
  Register register_2 (.D(or_3_out), .en(or_5_out), .Q(register_2_q), .clk(clock_2_out));  // open: clr
  assign controlled_buffer_4_out = Write ? SPL_EN : 1'bz;  // Controlled_Buffer controlled_buffer_4
  Pull_Resistor pull_resistor_4 (.node(controlled_buffer_4_out));
  or or_5 (or_5_out, controlled_buffer_4_out, or_8_out);
  Clock clock_2 (.out(clock_2_out));
  Shifter shifter_1 (.in(8'h1), .\dist (BitToMod), .out(shifter_1_out));
  assign and_1_out = shifter_1_out & DATA_IN;  // AND_Gate and_1, 8 bits wide
  assign controlled_buffer_5_out = not_3_out ? BM_EN : 1'bz;  // Controlled_Buffer controlled_buffer_5
  Pull_Resistor pull_resistor_5 (.node(controlled_buffer_5_out));
  Pull_Resistor pull_resistor_6 (.node(pull_resistor_6_node));
  assign pull_resistor_6_node = controlled_buffer_5_out ? DATA_IN : 8'bz;  // Controlled_Buffer controlled_buffer_6
  assign controlled_buffer_7_out = controlled_buffer_5_out ? SREG_IN : 8'bz;  // Controlled_Buffer controlled_buffer_7
  Pull_Resistor pull_resistor_7 (.node(pull_resistor_7_node));
  assign pull_resistor_7_node = Write ? SREG_EN : 1'bz;  // Controlled_Buffer controlled_buffer_8
  or or_6 (or_6_out, pull_resistor_7_node, SREG_ALU_EN);
  Pull_Resistor pull_resistor_8 (.node(DATA_OUT));
  Adder #(.width(16)) adder_1 (
    .a({register_1_q, register_2_q}), .b(controlled_buffer_1_out), .out({adder_1_out_2, adder_1_out}));  // open: cin, cout
  assign DATA_OUT = and_2_out ? register_1_q : 8'bz;  // Controlled_Buffer controlled_buffer_9
  and and_2 (and_2_out, SPH_EN, Read);
  assign DATA_OUT = and_3_out ? register_2_q : 8'bz;  // Controlled_Buffer controlled_buffer_10
  and and_3 (and_3_out, SPL_EN, Read);
  Comparator comparator_1 (.a(8'h1), .b(and_1_out), .eq(comparator_1_eq), .lt(comparator_1_lt));  // open: gt
  assign controlled_buffer_11_out = SREG_LDT ? bitmanipulator_2_modified : 8'bz;  // Controlled_Buffer controlled_buffer_11
  Pull_Resistor pull_resistor_9 (.node(controlled_buffer_11_out));
  not not_3 (not_3_out, SREG_LDT);
  assign or_7_out = controlled_buffer_11_out | BM_OUT | pull_resistor_6_node | controlled_buffer_7_out;  // OR_Gate or_7, 8 bits wide
  Pull_Resistor pull_resistor_10 (.node(controlled_buffer_7_out));
  Pull_Resistor pull_resistor_11 (.node(pull_resistor_11_node));
  assign pull_resistor_11_node = or_8_out ? {register_1_q, register_2_q} : 16'bz;  // Controlled_Buffer controlled_buffer_12
  or or_8 (or_8_out, SP_Push, SP_Pop);
  or or_9 (or_9_out, comparator_1_eq, comparator_1_lt);
  not not_4 (not_4_out, or_9_out);
  BitManipulator bitmanipulator_2 (
    .Modified(bitmanipulator_2_modified), .Bit(3'b110), .CLR(not_4_out), .SET(or_9_out), .Initial(SREG_OUT));
  Register register_3 (.D(or_7_out), .en(or_6_out), .Q(SREG_OUT), .clk(CLK));  // open: clr
  and and_4 (and_4_out, SREG_EN, Read);
  Adder #(.width(16)) adder_2 (
    .a(pull_resistor_11_node), .b(controlled_buffer_13_out), .out(SP_OUT));  // open: cin, cout
  assign controlled_buffer_13_out = SP_Pop ? 16'h1 : 16'bz;  // Controlled_Buffer controlled_buffer_13
  Pull_Resistor pull_resistor_12 (.node(controlled_buffer_13_out));
  assign DATA_OUT = and_4_out ? SREG_OUT : 8'bz;  // Controlled_Buffer controlled_buffer_14

  // Other names for the same wires on the sheet: Bits[2:0] = BitToMod; BM_IN[7:0] = DATA_OUT; RD = Read; WT = Write
endmodule

module PORT (
  input  [7:0] DATA_IN,
  input  Write,
  input  Read,
  input  PIN_En,
  input  DDR_En,
  input  PORT_En,
  input  [7:0] PORT_IN,
  output [7:0] PORT_OUT,
  output [7:0] DATA_OUT
);

  wire and_1_out, and_2_out, and_3_out, and_4_out, and_5_out, clock_1_out;
  wire [7:0] and_7_out, DDR_q, not_1_out, PIN_q, PORT_q;

  and and_1 (and_1_out, DDR_En, Write);
  and and_2 (and_2_out, PORT_En, Write);
  Pull_Resistor pull_resistor_1 (.node(DATA_OUT));
  and and_3 (and_3_out, Read, PIN_En);
  and and_4 (and_4_out, Read, DDR_En);
  and and_5 (and_5_out, Read, PORT_En);
  Clock clock_1 (.out(clock_1_out));
  Register DDR (.D(DATA_IN), .en(and_1_out), .Q(DDR_q), .clk(clock_1_out));  // open: clr
  assign DATA_OUT = and_4_out ? DDR_q : 8'bz;  // Controlled_Buffer controlled_buffer_1
  Register PORT (.D(DATA_IN), .en(and_2_out), .Q(PORT_q), .clk(clock_1_out));  // open: clr
  assign DATA_OUT = and_5_out ? PORT_q : 8'bz;  // Controlled_Buffer controlled_buffer_2
  Register PIN (.D(and_7_out), .en(clock_1_out), .Q(PIN_q), .clk(clock_1_out));  // open: clr
  assign DATA_OUT = and_3_out ? PIN_q : 8'bz;  // Controlled_Buffer controlled_buffer_3
  assign PORT_OUT = DDR_q & PORT_q;  // AND_Gate and_6, 8 bits wide
  assign not_1_out = ~DDR_q;  // NOT_Gate not_1, 8 bits wide
  assign and_7_out = not_1_out & PORT_IN;  // AND_Gate and_7, 8 bits wide
  Pull_Resistor pull_resistor_2 (.node(PORT_IN));
endmodule

// BM
module BitManipulator (
  input  [2:0] Bit,
  input  CLR,
  input  SET,
  input  [7:0] Initial,
  output [7:0] Modified
);

  wire [7:0] and_1_out, not_1_out, or_1_out, shifter_1_out;

  Pull_Resistor pull_resistor_1 (.node(Modified));
  Shifter shifter_1 (.in(8'h1), .\dist (Bit), .out(shifter_1_out));
  assign or_1_out = shifter_1_out | Initial;  // OR_Gate or_1, 8 bits wide
  assign Modified = SET ? or_1_out : 8'bz;  // Controlled_Buffer controlled_buffer_1
  assign and_1_out = Initial & not_1_out;  // AND_Gate and_1, 8 bits wide
  assign Modified = CLR ? and_1_out : 8'bz;  // Controlled_Buffer controlled_buffer_2
  assign not_1_out = ~shifter_1_out;  // NOT_Gate not_1, 8 bits wide
endmodule

module SRAM (
  input  [10:0] Addr_IN,
  input  [7:0] Data_IN,
  input  Write,
  input  Read,
  output [7:0] DATA_OUT
);

  wire clock_1_out;
  wire [7:0] ram_1_data;

  Clock clock_1 (.out(clock_1_out));
  RAM_part #(.addrWidth(11), .bus("separate")) ram_1 (
    .addr(Addr_IN), .din(Data_IN), .data(ram_1_data), .str(Write), .clk(clock_1_out), .ld(Read));  // open: sel, clr
  assign DATA_OUT = Read ? ram_1_data : 8'bz;  // Controlled_Buffer controlled_buffer_1
endmodule
