// Logisim project AVR2.circ as structural Verilog: 7 circuits, main circuit AVRCore
module AVRCore (
);

  wire [7:0] progcounter_1_bus_1_out, progcounter_1_bus_2_out;
  wire [15:0] flash_1_flash_out, instrreg_1_out, instrreg_1_to_dec, progcounter_1_pc_out;
  wire [31:0] decoder_1_ctrl_out;

  // Probe on progcounter_1_bus_1_out
  ProgCounter progcounter_1 (
    .Ctrl_IN(decoder_1_ctrl_out), .Instr_IN(instrreg_1_out), .Bus_1_IN(progcounter_1_bus_1_out),
    .Bus_2_IN(progcounter_1_bus_2_out), .Bus_1_OUT(progcounter_1_bus_1_out),
    .Bus_2_OUT(progcounter_1_bus_2_out), .PC_OUT(progcounter_1_pc_out));  // open: PC_2_OUT, IN
  // Probe on progcounter_1_bus_2_out
  // Probe on instrreg_1_out
  InstrReg instrreg_1 (.Instr_IN(flash_1_flash_out), .TO_DEC(instrreg_1_to_dec), .OUT(instrreg_1_out));
  Flash flash_1 (.PC_IN(progcounter_1_pc_out), .Flash_OUT(flash_1_flash_out));
  Decoder decoder_1 (.Instr_IN(instrreg_1_to_dec), .Ctrl_OUT(decoder_1_ctrl_out));
  // Probe on decoder_1_ctrl_out
endmodule

// FLASH
module Flash (
  input  [15:0] PC_IN,
  output [15:0] Flash_OUT
);

  ROM #(.addrWidth(16), .dataWidth(16)) rom_1 (.addr(PC_IN), .data(Flash_OUT));  // open: sel
endmodule

// DEC
module Decoder (
  input  [15:0] Instr_IN,
  output [31:0] Ctrl_OUT
);

  wire clock_1_out, comparator_1_eq;
  wire [7:0] controlled_buffer_1_out;
  wire [15:0] register_1_q;

  Register #(.width(16)) register_1 (.D(Instr_IN), .en(Ctrl_OUT[0]), .Q(register_1_q), .clk(clock_1_out));  // open: clr
  Clock clock_1 (.out(clock_1_out));
  Comparator #(.width(16), .mode("unsigned")) comparator_1 (
    .a(register_1_q), .b({16{1'b0}}), .eq(comparator_1_eq));  // open: gt, lt
  assign controlled_buffer_1_out = comparator_1_eq ? {8{1'b0}} : 8'bz;  // Controlled_Buffer controlled_buffer_1
  ROM #(.dataWidth(32)) rom_1 (.addr(controlled_buffer_1_out), .data(Ctrl_OUT));  // open: sel
endmodule

// INSTR
module InstrReg (
  input  [15:0] Instr_IN,
  output [15:0] OUT,
  output [15:0] TO_DEC
);

  wire clock_1_out;

  Clock clock_1 (.out(clock_1_out));
  Register #(.width(16), .trigger("high")) register_1 (.D(Instr_IN), .Q(OUT), .clk(clock_1_out));  // open: en, clr

  assign TO_DEC = OUT;
endmodule

// PC
module ProgCounter (
  input  [31:0] Ctrl_IN,
  input  [15:0] Instr_IN,
  input  [7:0] Bus_1_IN,
  input  [7:0] Bus_2_IN,
  input  [15:0] IN,
  output [7:0] Bus_1_OUT,
  output [7:0] Bus_2_OUT,
  output [15:0] PC_2_OUT,
  output [15:0] PC_OUT
);

  wire B1O, B2O, clock_1_out, or_1_out;
  wire [15:0] adder_2_out, adder_3_out, pull_resistor_1_node;

  Pull_Resistor pull_resistor_1 (.node(pull_resistor_1_node));
  Clock clock_1 (.out(clock_1_out));
  Adder #(.width(16)) adder_1 (.a({PC_OUT[15:8], Bus_1_IN}), .b(16'h1), .out(PC_2_OUT));  // open: cin, cout
  assign pull_resistor_1_node = Ctrl_IN[1] ? {PC_OUT[15:8], Bus_1_IN} : 16'bz;  // Controlled_Buffer controlled_buffer_1
  assign pull_resistor_1_node = Ctrl_IN[2] ? {Bus_1_IN, Bus_1_IN} : 16'bz;  // Controlled_Buffer controlled_buffer_2
  Counter #(.width(16), .max('hffff)) counter_1 (
    .load(or_1_out), .D(pull_resistor_1_node), .count(Ctrl_IN[0]), .Q({PC_OUT[15:8], Bus_1_IN}),
    .clk(clock_1_out));  // open: carry, clr
  assign pull_resistor_1_node = Ctrl_IN[3] ? IN : 16'bz;  // Controlled_Buffer controlled_buffer_3
  or or_1 (or_1_out, Ctrl_IN[1], Ctrl_IN[2], Ctrl_IN[3], Ctrl_IN[4]);
  assign pull_resistor_1_node = Ctrl_IN[4] ? adder_3_out : 16'bz;  // Controlled_Buffer controlled_buffer_4
  Adder #(.width(16)) adder_2 (.a({PC_OUT[15:8], Bus_1_IN}), .b(16'h1), .out(adder_2_out));  // open: cin, cout
  Adder #(.width(16)) adder_3 (.a(IN), .b(adder_2_out), .out(adder_3_out));  // open: cin, cout
  Controlled_Buffer #(.width(8)) controlled_buffer_5 (.out(Bus_1_OUT), .en(B1O));  // open: in
  Pull_Resistor pull_resistor_2 (.node(Bus_1_OUT));
  Pull_Resistor pull_resistor_3 (.node(B1O));
  Pull_Resistor pull_resistor_4 (.node(Bus_2_OUT));
  Controlled_Buffer #(.width(8)) controlled_buffer_6 (.out(Bus_2_OUT), .en(B2O));  // open: in
  Pull_Resistor pull_resistor_5 (.node(B2O));

  assign PC_OUT[7:0] = Bus_1_IN;
endmodule

module Device (
  input  [31:0] Ctrl_IN,
  input  [15:0] Instr_IN,
  input  [7:0] Bus_1_IN,
  input  [7:0] Bus_2_IN,
  output [7:0] Bus_1_OUT,
  output [7:0] Bus_2_OUT
);

  wire B1O, B2O;

  Controlled_Buffer #(.width(8)) controlled_buffer_1 (.out(Bus_1_OUT), .en(B1O));  // open: in
  Pull_Resistor pull_resistor_1 (.node(Bus_1_OUT));
  Pull_Resistor pull_resistor_2 (.node(B1O));
  Controlled_Buffer #(.width(8)) controlled_buffer_2 (.out(Bus_2_OUT), .en(B2O));  // open: in
  Pull_Resistor pull_resistor_3 (.node(Bus_2_OUT));
  Pull_Resistor pull_resistor_4 (.node(B2O));
endmodule

module RegFile (
  input  [31:0] Ctrl_IN,
  input  [15:0] Instr_IN,
  input  [7:0] Bus_1_IN,
  input  [7:0] Bus_2_IN,
  output [7:0] Bus_1_OUT,
  output [7:0] Bus_2_OUT,
  output [7:0] ALU_1,
  output [7:0] ALU_2,
  output [15:0] Pair_OUT
);

  wire B1O, B2O, clock_1_out, clock_2_out, clock_3_out, clock_4_out, clock_5_out, clock_6_out, clock_7_out,
       clock_8_out, clock_9_out, clock_10_out, clock_11_out, clock_12_out, clock_13_out, clock_14_out,
       clock_15_out, clock_16_out, clock_17_out, clock_18_out, clock_19_out, clock_20_out, clock_21_out,
       clock_22_out, clock_23_out, clock_24_out, clock_25_out, clock_26_out, clock_27_out, clock_28_out,
       clock_29_out, clock_30_out, clock_31_out, clock_32_out, not_1_out, not_2_out, or_1_out, or_2_out,
       or_3_out, r0rd, r0rr, r0w, r1rd, r1rr, r1w, r2rd, r2rr, r2w, r3rd, r3rr, r3w, r4rd, r4rr, r4w, r5rd,
       r5rr, r5w, r6rd, r6rr, r6w, r7rd, r7rr, r7w, r8rd, r8rr, r8w, r9rd, r9rr, r9w, r10rd, r10rr, r10w,
       r11rd, r11rr, r11w, r12rd, r12rr, r12w, r13rd, r13rr, r13w, r14rd, r14rr, r14w, r15rd, r15rr, r15w,
       r16rd, r16rr, r16w, r17rd, r17rr, r17w, r18rd, r18rr, r18w, r19rd, r19rr, r19w, r20rd, r20rr, r20w,
       r21rd, r21rr, r21w, r22rd, r22rr, r22w, r23rd, r23rr, r23w, r24rd, r24rr, r24w, r25rd, r25rr, r25w,
       r26rd, r26rr, r26w, r27rd, r27rr, r27w, r28rd, r28rr, r28w, r29rd, r29rr, r29w, r30rd, r30rr, r30w,
       r31rd, r31rr, r31w;
  wire [4:0] adder_1_out, controlled_buffer_98_out, controlled_buffer_99_out, or_4_out;
  wire [7:0] controlled_buffer_2_out, controlled_buffer_5_out, controlled_buffer_8_out,
       controlled_buffer_11_out, controlled_buffer_14_out, controlled_buffer_17_out,
       controlled_buffer_20_out, controlled_buffer_23_out, controlled_buffer_25_out,
       controlled_buffer_26_out, controlled_buffer_27_out, controlled_buffer_28_out,
       controlled_buffer_29_out, controlled_buffer_30_out, controlled_buffer_31_out,
       controlled_buffer_32_out, controlled_buffer_49_out, controlled_buffer_50_out,
       controlled_buffer_51_out, controlled_buffer_52_out, controlled_buffer_53_out,
       controlled_buffer_54_out, controlled_buffer_55_out, controlled_buffer_56_out,
       controlled_buffer_73_out, controlled_buffer_74_out, controlled_buffer_75_out,
       controlled_buffer_76_out, controlled_buffer_77_out, controlled_buffer_78_out,
       controlled_buffer_79_out, controlled_buffer_80_out, register_1_q, register_2_q, register_3_q,
       register_4_q, register_5_q, register_6_q, register_7_q, register_8_q, register_9_q, register_10_q,
       register_11_q, register_12_q, register_13_q, register_14_q, register_15_q, register_16_q,
       register_17_q, register_18_q, register_19_q, register_20_q, register_21_q, register_22_q,
       register_23_q, register_24_q, register_25_q, register_26_q, register_27_q, register_28_q,
       register_29_q, register_30_q, register_31_q, register_32_q;

  assign ALU_2 = r0rr ? register_1_q : 8'bz;  // Controlled_Buffer controlled_buffer_1
  assign controlled_buffer_2_out = r0w ? Bus_1_IN : 8'bz;  // Controlled_Buffer controlled_buffer_2
  Register register_1 (.D(controlled_buffer_2_out), .en(r0w), .Q(register_1_q), .clk(clock_1_out));  // open: clr
  assign ALU_1 = r0rd ? register_1_q : 8'bz;  // Controlled_Buffer controlled_buffer_3
  Clock clock_1 (.out(clock_1_out));
  assign ALU_2 = r4rr ? register_2_q : 8'bz;  // Controlled_Buffer controlled_buffer_4
  Register register_2 (.D(controlled_buffer_5_out), .en(r4w), .Q(register_2_q), .clk(clock_2_out));  // open: clr
  assign controlled_buffer_5_out = r4w ? Bus_1_IN : 8'bz;  // Controlled_Buffer controlled_buffer_5
  assign ALU_1 = r4rd ? register_2_q : 8'bz;  // Controlled_Buffer controlled_buffer_6
  Clock clock_2 (.out(clock_2_out));
  assign ALU_2 = r8rr ? register_3_q : 8'bz;  // Controlled_Buffer controlled_buffer_7
  Register register_3 (.D(controlled_buffer_8_out), .en(r8w), .Q(register_3_q), .clk(clock_3_out));  // open: clr
  assign controlled_buffer_8_out = r8w ? Bus_1_IN : 8'bz;  // Controlled_Buffer controlled_buffer_8
  assign ALU_1 = r8rd ? register_3_q : 8'bz;  // Controlled_Buffer controlled_buffer_9
  Clock clock_3 (.out(clock_3_out));
  assign ALU_2 = r12rr ? register_4_q : 8'bz;  // Controlled_Buffer controlled_buffer_10
  Register register_4 (.D(controlled_buffer_11_out), .en(r12w), .Q(register_4_q), .clk(clock_4_out));  // open: clr
  assign controlled_buffer_11_out = r12w ? Bus_1_IN : 8'bz;  // Controlled_Buffer controlled_buffer_11
  assign ALU_1 = r12rd ? register_4_q : 8'bz;  // Controlled_Buffer controlled_buffer_12
  Clock clock_4 (.out(clock_4_out));
  assign ALU_2 = r16rr ? register_5_q : 8'bz;  // Controlled_Buffer controlled_buffer_13
  assign controlled_buffer_14_out = r16w ? Bus_1_IN : 8'bz;  // Controlled_Buffer controlled_buffer_14
  Register register_5 (.D(controlled_buffer_14_out), .en(r16w), .Q(register_5_q), .clk(clock_5_out));  // open: clr
  assign ALU_1 = r16rd ? register_5_q : 8'bz;  // Controlled_Buffer controlled_buffer_15
  Clock clock_5 (.out(clock_5_out));
  assign ALU_2 = r20rr ? register_6_q : 8'bz;  // Controlled_Buffer controlled_buffer_16
  Register register_6 (.D(controlled_buffer_17_out), .en(r20w), .Q(register_6_q), .clk(clock_6_out));  // open: clr
  assign controlled_buffer_17_out = r20w ? Bus_1_IN : 8'bz;  // Controlled_Buffer controlled_buffer_17
  assign ALU_1 = r20rd ? register_6_q : 8'bz;  // Controlled_Buffer controlled_buffer_18
  Clock clock_6 (.out(clock_6_out));
  assign ALU_2 = r24rr ? register_7_q : 8'bz;  // Controlled_Buffer controlled_buffer_19
  Register register_7 (.D(controlled_buffer_20_out), .en(r24w), .Q(register_7_q), .clk(clock_7_out));  // open: clr
  assign controlled_buffer_20_out = r24w ? Bus_1_IN : 8'bz;  // Controlled_Buffer controlled_buffer_20
  assign ALU_1 = r24rd ? register_7_q : 8'bz;  // Controlled_Buffer controlled_buffer_21
  Clock clock_7 (.out(clock_7_out));
  assign ALU_2 = r28rr ? register_8_q : 8'bz;  // Controlled_Buffer controlled_buffer_22
  assign controlled_buffer_23_out = r28w ? Bus_1_IN : 8'bz;  // Controlled_Buffer controlled_buffer_23
  Register register_8 (.D(controlled_buffer_23_out), .en(r28w), .Q(register_8_q), .clk(clock_8_out));  // open: clr
  assign ALU_1 = r28rd ? register_8_q : 8'bz;  // Controlled_Buffer controlled_buffer_24
  Clock clock_8 (.out(clock_8_out));
  Register register_9 (.D(controlled_buffer_25_out), .en(r1w), .Q(register_9_q), .clk(clock_9_out));  // open: clr
  assign controlled_buffer_25_out = r1w ? Bus_1_IN : 8'bz;  // Controlled_Buffer controlled_buffer_25
  Clock clock_9 (.out(clock_9_out));
  Register register_10 (.D(controlled_buffer_26_out), .en(r5w), .Q(register_10_q), .clk(clock_10_out));  // open: clr
  assign controlled_buffer_26_out = r5w ? Bus_1_IN : 8'bz;  // Controlled_Buffer controlled_buffer_26
  Clock clock_10 (.out(clock_10_out));
  Register register_11 (.D(controlled_buffer_27_out), .en(r9w), .Q(register_11_q), .clk(clock_11_out));  // open: clr
  assign controlled_buffer_27_out = r9w ? Bus_1_IN : 8'bz;  // Controlled_Buffer controlled_buffer_27
  Clock clock_11 (.out(clock_11_out));
  assign controlled_buffer_28_out = r13w ? Bus_1_IN : 8'bz;  // Controlled_Buffer controlled_buffer_28
  Register register_12 (.D(controlled_buffer_28_out), .en(r13w), .Q(register_12_q), .clk(clock_12_out));  // open: clr
  Clock clock_12 (.out(clock_12_out));
  assign controlled_buffer_29_out = r17w ? Bus_1_IN : 8'bz;  // Controlled_Buffer controlled_buffer_29
  Register register_13 (.D(controlled_buffer_29_out), .en(r17w), .Q(register_13_q), .clk(clock_13_out));  // open: clr
  Clock clock_13 (.out(clock_13_out));
  assign controlled_buffer_30_out = r21w ? Bus_1_IN : 8'bz;  // Controlled_Buffer controlled_buffer_30
  Register register_14 (.D(controlled_buffer_30_out), .en(r21w), .Q(register_14_q), .clk(clock_14_out));  // open: clr
  Clock clock_14 (.out(clock_14_out));
  assign controlled_buffer_31_out = r25w ? Bus_1_IN : 8'bz;  // Controlled_Buffer controlled_buffer_31
  Register register_15 (.D(controlled_buffer_31_out), .en(r25w), .Q(register_15_q), .clk(clock_15_out));  // open: clr
  Clock clock_15 (.out(clock_15_out));
  Register register_16 (.D(controlled_buffer_32_out), .en(r29w), .Q(register_16_q), .clk(clock_16_out));  // open: clr
  assign controlled_buffer_32_out = r29w ? Bus_1_IN : 8'bz;  // Controlled_Buffer controlled_buffer_32
  Clock clock_16 (.out(clock_16_out));
  assign ALU_2 = r1rr ? register_9_q : 8'bz;  // Controlled_Buffer controlled_buffer_33
  assign ALU_1 = r1rd ? register_9_q : 8'bz;  // Controlled_Buffer controlled_buffer_34
  assign ALU_2 = r5rr ? register_10_q : 8'bz;  // Controlled_Buffer controlled_buffer_35
  assign ALU_1 = r5rd ? register_10_q : 8'bz;  // Controlled_Buffer controlled_buffer_36
  assign ALU_2 = r9rr ? register_11_q : 8'bz;  // Controlled_Buffer controlled_buffer_37
  assign ALU_1 = r9rd ? register_11_q : 8'bz;  // Controlled_Buffer controlled_buffer_38
  assign ALU_2 = r13rr ? register_12_q : 8'bz;  // Controlled_Buffer controlled_buffer_39
  assign ALU_1 = r13rd ? register_12_q : 8'bz;  // Controlled_Buffer controlled_buffer_40
  assign ALU_2 = r17rr ? register_13_q : 8'bz;  // Controlled_Buffer controlled_buffer_41
  assign ALU_1 = r17rd ? register_13_q : 8'bz;  // Controlled_Buffer controlled_buffer_42
  assign ALU_2 = r21rr ? register_14_q : 8'bz;  // Controlled_Buffer controlled_buffer_43
  assign ALU_1 = r21rd ? register_14_q : 8'bz;  // Controlled_Buffer controlled_buffer_44
  assign ALU_2 = r25rr ? register_15_q : 8'bz;  // Controlled_Buffer controlled_buffer_45
  assign ALU_1 = r25rd ? register_15_q : 8'bz;  // Controlled_Buffer controlled_buffer_46
  assign ALU_2 = r29rr ? register_16_q : 8'bz;  // Controlled_Buffer controlled_buffer_47
  assign ALU_1 = r29rd ? register_16_q : 8'bz;  // Controlled_Buffer controlled_buffer_48
  Pull_Resistor pull_resistor_1 (.node(ALU_1));
  assign controlled_buffer_49_out = r2w ? Bus_1_IN : 8'bz;  // Controlled_Buffer controlled_buffer_49
  Clock clock_17 (.out(clock_17_out));
  assign controlled_buffer_50_out = r6w ? Bus_1_IN : 8'bz;  // Controlled_Buffer controlled_buffer_50
  Clock clock_18 (.out(clock_18_out));
  assign controlled_buffer_51_out = r10w ? Bus_1_IN : 8'bz;  // Controlled_Buffer controlled_buffer_51
  Clock clock_19 (.out(clock_19_out));
  assign controlled_buffer_52_out = r14w ? Bus_1_IN : 8'bz;  // Controlled_Buffer controlled_buffer_52
  Clock clock_20 (.out(clock_20_out));
  assign controlled_buffer_53_out = r18w ? Bus_1_IN : 8'bz;  // Controlled_Buffer controlled_buffer_53
  Clock clock_21 (.out(clock_21_out));
  assign controlled_buffer_54_out = r22w ? Bus_1_IN : 8'bz;  // Controlled_Buffer controlled_buffer_54
  Clock clock_22 (.out(clock_22_out));
  assign controlled_buffer_55_out = r26w ? Bus_1_IN : 8'bz;  // Controlled_Buffer controlled_buffer_55
  Clock clock_23 (.out(clock_23_out));
  assign controlled_buffer_56_out = r30w ? Bus_1_IN : 8'bz;  // Controlled_Buffer controlled_buffer_56
  Clock clock_24 (.out(clock_24_out));
  Pull_Resistor pull_resistor_2 (.node(ALU_2));
  assign ALU_2 = r2rr ? register_17_q : 8'bz;  // Controlled_Buffer controlled_buffer_57
  Register register_17 (.D(controlled_buffer_49_out), .en(r2w), .Q(register_17_q), .clk(clock_17_out));  // open: clr
  assign ALU_1 = r2rd ? register_17_q : 8'bz;  // Controlled_Buffer controlled_buffer_58
  assign ALU_2 = r6rr ? register_18_q : 8'bz;  // Controlled_Buffer controlled_buffer_59
  Register register_18 (.D(controlled_buffer_50_out), .en(r6w), .Q(register_18_q), .clk(clock_18_out));  // open: clr
  assign ALU_1 = r6rd ? register_18_q : 8'bz;  // Controlled_Buffer controlled_buffer_60
  assign ALU_2 = r10rr ? register_19_q : 8'bz;  // Controlled_Buffer controlled_buffer_61
  Register register_19 (.D(controlled_buffer_51_out), .en(r10w), .Q(register_19_q), .clk(clock_19_out));  // open: clr
  assign ALU_1 = r10rd ? register_19_q : 8'bz;  // Controlled_Buffer controlled_buffer_62
  assign ALU_2 = r14rr ? register_20_q : 8'bz;  // Controlled_Buffer controlled_buffer_63
  Register register_20 (.D(controlled_buffer_52_out), .en(r14w), .Q(register_20_q), .clk(clock_20_out));  // open: clr
  assign ALU_1 = r14rd ? register_20_q : 8'bz;  // Controlled_Buffer controlled_buffer_64
  assign ALU_2 = r18rr ? register_21_q : 8'bz;  // Controlled_Buffer controlled_buffer_65
  Register register_21 (.D(controlled_buffer_53_out), .en(r18w), .Q(register_21_q), .clk(clock_21_out));  // open: clr
  assign ALU_1 = r18rd ? register_21_q : 8'bz;  // Controlled_Buffer controlled_buffer_66
  assign ALU_2 = r22rr ? register_22_q : 8'bz;  // Controlled_Buffer controlled_buffer_67
  Register register_22 (.D(controlled_buffer_54_out), .en(r22w), .Q(register_22_q), .clk(clock_22_out));  // open: clr
  assign ALU_1 = r22rd ? register_22_q : 8'bz;  // Controlled_Buffer controlled_buffer_68
  assign ALU_2 = r26rr ? register_23_q : 8'bz;  // Controlled_Buffer controlled_buffer_69
  Register register_23 (.D(controlled_buffer_55_out), .en(r26w), .Q(register_23_q), .clk(clock_23_out));  // open: clr
  assign ALU_1 = r26rd ? register_23_q : 8'bz;  // Controlled_Buffer controlled_buffer_70
  assign ALU_2 = r30rr ? register_24_q : 8'bz;  // Controlled_Buffer controlled_buffer_71
  Register register_24 (.D(controlled_buffer_56_out), .en(r30w), .Q(register_24_q), .clk(clock_24_out));  // open: clr
  assign ALU_1 = r30rd ? register_24_q : 8'bz;  // Controlled_Buffer controlled_buffer_72
  assign controlled_buffer_73_out = r3w ? Bus_1_IN : 8'bz;  // Controlled_Buffer controlled_buffer_73
  assign controlled_buffer_74_out = r7w ? Bus_1_IN : 8'bz;  // Controlled_Buffer controlled_buffer_74
  assign controlled_buffer_75_out = r11w ? Bus_1_IN : 8'bz;  // Controlled_Buffer controlled_buffer_75
  assign controlled_buffer_76_out = r15w ? Bus_1_IN : 8'bz;  // Controlled_Buffer controlled_buffer_76
  assign controlled_buffer_77_out = r19w ? Bus_1_IN : 8'bz;  // Controlled_Buffer controlled_buffer_77
  assign controlled_buffer_78_out = r23w ? Bus_1_IN : 8'bz;  // Controlled_Buffer controlled_buffer_78
  assign controlled_buffer_79_out = r27w ? Bus_1_IN : 8'bz;  // Controlled_Buffer controlled_buffer_79
  assign controlled_buffer_80_out = r31w ? Bus_1_IN : 8'bz;  // Controlled_Buffer controlled_buffer_80
  assign Pair_OUT = Ctrl_IN[11] ? {ALU_2, ALU_1} : 16'bz;  // Controlled_Buffer controlled_buffer_81
  assign ALU_2 = r3rr ? register_25_q : 8'bz;  // Controlled_Buffer controlled_buffer_82
  Register register_25 (.D(controlled_buffer_73_out), .en(r3w), .Q(register_25_q), .clk(clock_25_out));  // open: clr
  assign ALU_1 = r3rd ? register_25_q : 8'bz;  // Controlled_Buffer controlled_buffer_83
  Clock clock_25 (.out(clock_25_out));
  assign ALU_2 = r7rr ? register_26_q : 8'bz;  // Controlled_Buffer controlled_buffer_84
  Register register_26 (.D(controlled_buffer_74_out), .en(r7w), .Q(register_26_q), .clk(clock_26_out));  // open: clr
  assign ALU_1 = r7rd ? register_26_q : 8'bz;  // Controlled_Buffer controlled_buffer_85
  Clock clock_26 (.out(clock_26_out));
  assign ALU_2 = r11rr ? register_27_q : 8'bz;  // Controlled_Buffer controlled_buffer_86
  Register register_27 (.D(controlled_buffer_75_out), .en(r11w), .Q(register_27_q), .clk(clock_27_out));  // open: clr
  assign ALU_1 = r11rd ? register_27_q : 8'bz;  // Controlled_Buffer controlled_buffer_87
  Clock clock_27 (.out(clock_27_out));
  assign ALU_2 = r15rr ? register_28_q : 8'bz;  // Controlled_Buffer controlled_buffer_88
  Register register_28 (.D(controlled_buffer_76_out), .en(r15w), .Q(register_28_q), .clk(clock_28_out));  // open: clr
  assign ALU_1 = r15rd ? register_28_q : 8'bz;  // Controlled_Buffer controlled_buffer_89
  Clock clock_28 (.out(clock_28_out));
  assign ALU_2 = r19rr ? register_29_q : 8'bz;  // Controlled_Buffer controlled_buffer_90
  Register register_29 (.D(controlled_buffer_77_out), .en(r19w), .Q(register_29_q), .clk(clock_29_out));  // open: clr
  assign ALU_1 = r19rd ? register_29_q : 8'bz;  // Controlled_Buffer controlled_buffer_91
  Clock clock_29 (.out(clock_29_out));
  assign ALU_2 = r23rr ? register_30_q : 8'bz;  // Controlled_Buffer controlled_buffer_92
  Register register_30 (.D(controlled_buffer_78_out), .en(r23w), .Q(register_30_q), .clk(clock_30_out));  // open: clr
  assign ALU_1 = r23rd ? register_30_q : 8'bz;  // Controlled_Buffer controlled_buffer_93
  Clock clock_30 (.out(clock_30_out));
  assign ALU_2 = r27rr ? register_31_q : 8'bz;  // Controlled_Buffer controlled_buffer_94
  Register register_31 (.D(controlled_buffer_79_out), .en(r27w), .Q(register_31_q), .clk(clock_31_out));  // open: clr
  assign ALU_1 = r27rd ? register_31_q : 8'bz;  // Controlled_Buffer controlled_buffer_95
  Clock clock_31 (.out(clock_31_out));
  assign ALU_2 = r31rr ? register_32_q : 8'bz;  // Controlled_Buffer controlled_buffer_96
  Register register_32 (.D(controlled_buffer_80_out), .en(r31w), .Q(register_32_q), .clk(clock_32_out));  // open: clr
  assign ALU_1 = r31rd ? register_32_q : 8'bz;  // Controlled_Buffer controlled_buffer_97
  Clock clock_32 (.out(clock_32_out));
  or or_1 (or_1_out, Ctrl_IN[9], Ctrl_IN[11]);
  Decoder_part #(.select(5), .disabled(0)) decoder_1 (
    .out0(r0w), .out1(r1w), .out2(r2w), .out3(r3w), .out4(r4w), .out5(r5w), .out6(r6w), .out7(r7w),
    .out8(r8w), .out9(r9w), .out10(r10w), .out11(r11w), .out12(r12w), .out13(r13w), .out14(r14w),
    .out15(r15w), .out16(r16w), .out17(r17w), .out18(r18w), .out19(r19w), .out20(r20w), .out21(r21w),
    .out22(r22w), .out23(r23w), .out24(r24w), .out25(r25w), .out26(r26w), .out27(r27w), .out28(r28w),
    .out29(r29w), .out30(r30w), .out31(r31w), .sel(controlled_buffer_98_out), .en(Ctrl_IN[7]));
  Decoder_part #(.select(5), .disabled(0)) decoder_2 (
    .out0(r0rd), .out1(r1rd), .out2(r2rd), .out3(r3rd), .out4(r4rd), .out5(r5rd), .out6(r6rd), .out7(r7rd),
    .out8(r8rd), .out9(r9rd), .out10(r10rd), .out11(r11rd), .out12(r12rd), .out13(r13rd), .out14(r14rd),
    .out15(r15rd), .out16(r16rd), .out17(r17rd), .out18(r18rd), .out19(r19rd), .out20(r20rd), .out21(r21rd),
    .out22(r22rd), .out23(r23rd), .out24(r24rd), .out25(r25rd), .out26(r26rd), .out27(r27rd), .out28(r28rd),
    .out29(r29rd), .out30(r30rd), .out31(r31rd), .sel(Instr_IN[8:4]), .en(or_2_out));
  Decoder_part #(.select(5), .disabled(0)) decoder_3 (
    .out0(r0rr), .out1(r1rr), .out2(r2rr), .out3(r3rr), .out4(r4rr), .out5(r5rr), .out6(r6rr), .out7(r7rr),
    .out8(r8rr), .out9(r9rr), .out10(r10rr), .out11(r11rr), .out12(r12rr), .out13(r13rr), .out14(r14rr),
    .out15(r15rr), .out16(r16rr), .out17(r17rr), .out18(r18rr), .out19(r19rr), .out20(r20rr), .out21(r21rr),
    .out22(r22rr), .out23(r23rr), .out24(r24rr), .out25(r25rr), .out26(r26rr), .out27(r27rr), .out28(r28rr),
    .out29(r29rr), .out30(r30rr), .out31(r31rr), .sel(controlled_buffer_99_out), .en(or_1_out));
  or or_2 (or_2_out, Ctrl_IN[8], Ctrl_IN[11]);
  or or_3 (or_3_out, Ctrl_IN[10], Ctrl_IN[12]);
  not not_1 (not_1_out, or_3_out);
  assign controlled_buffer_98_out = Ctrl_IN[10] ? or_4_out : 5'bz;  // Controlled_Buffer controlled_buffer_98
  assign or_4_out = 5'b10000 | Instr_IN[8:4];  // OR_Gate or_4, 5 bits wide
  not not_2 (not_2_out, Ctrl_IN[11]);
  assign controlled_buffer_99_out = not_2_out ? {Instr_IN[9], Instr_IN[3:0]} : 5'bz;  // Controlled_Buffer controlled_buffer_99
  assign controlled_buffer_99_out = Ctrl_IN[11] ? adder_1_out : 5'bz;  // Controlled_Buffer controlled_buffer_100
  assign controlled_buffer_98_out = not_1_out ? Instr_IN[8:4] : 5'bz;  // Controlled_Buffer controlled_buffer_101
  assign controlled_buffer_98_out = Ctrl_IN[12] ? adder_1_out : 5'bz;  // Controlled_Buffer controlled_buffer_102
  Adder #(.width(5)) adder_1 (.a(Instr_IN[8:4]), .b(5'b00001), .out(adder_1_out));  // open: cin, cout
  Pull_Resistor pull_resistor_3 (.node(Bus_1_OUT));
  Controlled_Buffer #(.width(8)) controlled_buffer_103 (.out(Bus_1_OUT), .en(B1O));  // open: in
  Pull_Resistor pull_resistor_4 (.node(B1O));
  Controlled_Buffer #(.width(8)) controlled_buffer_104 (.out(Bus_2_OUT), .en(B2O));  // open: in
  Pull_Resistor pull_resistor_5 (.node(Bus_2_OUT));
  Pull_Resistor pull_resistor_6 (.node(B2O));

  // Other names for the same wires on the sheet: Rd[7:0] = ALU_1; Rr[7:0] = ALU_2; d[7:0] = Bus_1_IN
endmodule
